// Logisim project logisimPiloto.circ as structural Verilog
module main (
);

  wire button_2_out, button_3_out, button_4_out, button_out, clock_1_out, P_out, S_out;
  wire [3:0] videogame_1_s0, videogame_1_s1, videogame_1_s2, videogame_1_s3;

  Button button (.out(button_out));
  Button button_2 (.out(button_2_out));
  DotMatrix #(.matrixcols(4), .matrixrows(4)) dotmatrix_1 (
    .col0(videogame_1_s0), .col1(videogame_1_s1), .col2(videogame_1_s2), .col3(videogame_1_s3));
  Button button_3 (.out(button_3_out));
  Button button_4 (.out(button_4_out));
  Button P (.out(P_out));
  Button S (.out(S_out));
  Videogame videogame_1 (
    .in_2(button_3_out), .S0(videogame_1_s0), .S1(videogame_1_s1), .S2(videogame_1_s2), .S3(videogame_1_s3),
    .S(S_out), .P(P_out), .in_3(button_4_out), .in_4(button_2_out), .in_5(button_out), .CLK(clock_1_out));
  Clock clock_1 (.out(clock_1_out));
endmodule

module Videogame (
  input  CLK,
  input  in_2,
  input  in_3,
  input  in_4,
  input  in_5,
  input  S,
  input  P,
  output [3:0] S0,
  output [3:0] S1,
  output [3:0] S2,
  output [3:0] S3
);

  Contolador contolador_1 (
    .in_1(CLK), .in_2(S), .in_3(in_2), .in_4(in_3), .in_5(in_4), .in_6(in_5), .out_7(S0), .out_8(S1),
    .out_9(S2), .out_10(S3));
endmodule

module Contolador (
  input  in_1,
  input  in_2,
  input  in_3,
  input  in_4,
  input  in_5,
  input  in_6,
  output [3:0] out_7,
  output [3:0] out_8,
  output [3:0] out_9,
  output [3:0] out_10
);

  wire and_1_out, and_2_out, and_3_out, and_4_out, and_5_out, and_6_out, and_7_out, and_8_out, and_9_out,
       and_10_out, and_11_out, and_13_out, and_14_out, animacao_morte_1_out_7,
       codificador_do_display_1_out_12, counter_1_q, counter_4_q, d_ff_1_q, d_ff_2_q, d_ff_5_q, d_ff_6_q,
       d_ff_7_q, not_1_out, not_2_out, not_3_out, not_4_out, not_5_out, not_6_out, not_7_out, not_8_out,
       not_9_out, not_10_out, not_11_out, not_12_out, not_13_out, not_14_out, not_15_out;
  wire [0:0] and_12_out, j_k_ff_1_q;
  wire [1:0] d_ff_3_q;
  wire [2:0] animacao_morte_1_t, \input ;
  wire [3:0] adder_1_out, adder_2_out, animacao_morte_1_y, Comida_out_6, counter_3_q,
       \Estado_da_máquina_out_6 , \lista_de_memória_1_out_6 , \lista_de_memória_2_out_6 , multiplexer_1_out,
       multiplexer_2_out, multiplexer_3_out, multiplexer_4_out, multiplexer_6_out, multiplexer_7_out,
       multiplexer_9_out, multiplexer_10_out, multiplexer_12_out, multiplexer_15_out, multiplexer_16_out,
       Ponteiro_cabeca_out_6, Ponteiro_cauda_out_6, random_1_out, random_2_out, random_3_out,
       subtractor_1_out, subtractor_2_out, undriven, undriven_2, undriven_3, undriven_4, xnor_1_out,
       xnor_2_out, xnor_3_out, xnor_4_out;
  wire [5:0] multiplexer_8_out, multiplexer_11_out, multiplexer_13_out;
  wire [6:3] Posicoes_da_cobrinha_out_6;
  wire [7:0] counter_2_q;
  wire [7:4] calculo_nova_posicao_1_out_3;
  wire [9:0] multiplexer_5_out;
  wire [11:0] multiplexer_14_out, multiplexer_17_out;

  not not_1 (not_1_out, in_2);
  Random #(.width(4)) random_1 (.clk(in_1), .out(random_1_out));  // open: next, clr
  Random #(.width(4), .seed(1)) random_2 (.clk(in_1), .out(random_2_out));  // open: next, clr
  not not_2 (not_2_out, and_1_out);
  and and_1 (and_1_out, \Estado_da_máquina_out_6 [0], \Estado_da_máquina_out_6 [1], not_3_out, not_4_out);
  not not_3 (not_3_out, \Estado_da_máquina_out_6 [2]);
  not not_4 (not_4_out, \Estado_da_máquina_out_6 [3]);
  J_K_Flip_Flop j_k_ff_1 (.J(in_2), .clk(in_1), .K(not_1_out), .Q(j_k_ff_1_q[0]));  // open: Qn, preset, en, reset
  assign xnor_1_out = ~(random_1_out ^ random_2_out);  // XNOR_Gate xnor_1, 4 bits wide
  Counter #(.width(1), .max('h1)) counter_1 (
    .Q(counter_1_q), .clk(in_1), .clr(\Estado_da_máquina_out_6 [0]));  // open: load, D, count, carry
  Counter counter_2 (.Q(counter_2_q), .clk(in_1), .clr(not_2_out));  // open: load, D, count, carry
  and and_2 (and_2_out, xnor_1_out[0], xnor_1_out[1], xnor_1_out[2], xnor_1_out[3]);
  D_Flip_Flop d_ff_1 (.clk(\input [0]), .D(\input [1]), .Q(d_ff_1_q));  // open: Qn, preset, en, reset
  D_Flip_Flop d_ff_2 (.clk(\input [0]), .D(\input [2]), .Q(d_ff_2_q));  // open: Qn, preset, en, reset
  Multiplexer #(.width(4)) multiplexer_1 (
    .in0(4'b0010), .in1(4'b0001), .out(multiplexer_1_out), .sel(and_2_out));  // open: en
  Multiplexer #(.width(4)) multiplexer_2 (
    .in0(4'b0010), .in1(4'b0011), .out(multiplexer_2_out), .sel(counter_1_q));  // open: en
  D_Flip_Flop d_ff_3 (.clk(and_3_out), .D(d_ff_1_q), .Q(d_ff_3_q[0]));  // open: Qn, preset, en, reset
  D_Flip_Flop d_ff_4 (.clk(and_3_out), .D(d_ff_2_q), .Q(d_ff_3_q[1]));  // open: Qn, preset, en, reset
  and and_3 (and_3_out, counter_2_q[0], counter_2_q[1], counter_2_q[2], counter_2_q[3], counter_2_q[4], counter_2_q[5], counter_2_q[6], counter_2_q[7]);
  Multiplexer #(.width(4)) multiplexer_3 (
    .in0(4'b0011), .in1(4'b0100), .out(multiplexer_3_out), .sel(and_3_out));  // open: en
  Multiplexer #(.select(4), .width(4)) multiplexer_4 (
    .in0({3'b000, j_k_ff_1_q[0]}), .in1(multiplexer_1_out), .in2(multiplexer_2_out), .in3(multiplexer_3_out),
    .in4(4'b0101), .in5(multiplexer_9_out), .in6(4'b0111), .in7(multiplexer_12_out), .in8(4'b1001),
    .in9(multiplexer_10_out), .in10(4'b0011), .in14(multiplexer_16_out), .out(multiplexer_4_out),
    .sel(\Estado_da_máquina_out_6 ));  // open: in11, in12, in13, in15, en
  not not_5 (not_5_out, \Estado_da_máquina_out_6 [0]);
  not not_6 (not_6_out, \Estado_da_máquina_out_6 [1]);
  not not_7 (not_7_out, \Estado_da_máquina_out_6 [3]);
  \Lista_de_memória  \Estado_da_máquina  (
    .Adress(4'b0000), .Writing(multiplexer_4_out), .Write_enable(1'b1), .Reset(1'b0), .CLK(in_1),
    .out_6(\Estado_da_máquina_out_6 ));
  and and_4 (and_4_out, not_5_out, not_6_out, \Estado_da_máquina_out_6 [2], not_7_out);
  \Lista_de_memória  \lista_de_memória_1  (
    .Adress(4'b0000), .Writing(Posicoes_da_cobrinha_out_6), .Write_enable(and_4_out), .Reset(1'b0),
    .CLK(in_1), .out_6(\lista_de_memória_1_out_6 ));
  Calculo_nova_posicao calculo_nova_posicao_1 (
    .in_1(\lista_de_memória_1_out_6 ), .in_2(d_ff_3_q), .out_3(calculo_nova_posicao_1_out_3));
  not not_8 (not_8_out, \Estado_da_máquina_out_6 [1]);
  and and_5 (and_5_out, \Estado_da_máquina_out_6 [0], not_8_out, \Estado_da_máquina_out_6 [2], not_9_out);
  not not_9 (not_9_out, \Estado_da_máquina_out_6 [3]);
  Multiplexer #(.select(4), .width(10)) multiplexer_5 (
    .in1({2'b01, random_1_out, 4'b0000}), .in2({10{1'b0}}), .in4({{6{1'b0}}, Ponteiro_cabeca_out_6}),
    .in5({{6{1'b0}}, subtractor_1_out}), .in6({2'b01, calculo_nova_posicao_1_out_3, adder_1_out}),
    .in7({{6{1'b0}}, multiplexer_15_out}), .in8({2'b01, calculo_nova_posicao_1_out_3, adder_1_out}),
    .out(multiplexer_5_out), .sel(\Estado_da_máquina_out_6 ));  // open: in0, in3, in9, in10, in11, in12, in13, in14, in15, en
  Counter #(.width(4), .max('hf)) counter_3 (
    .Q(counter_3_q), .clk(and_6_out), .clr(d_ff_6_q));  // open: load, D, count, carry
  and and_6 (and_6_out, in_1, d_ff_5_q);
  D_Flip_Flop d_ff_5 (.clk(in_1), .D(and_7_out), .Q(d_ff_5_q));  // open: Qn, preset, en, reset
  and and_7 (and_7_out, and_5_out, not_10_out);
  and and_8 (and_8_out, and_5_out, and_11_out);
  not not_10 (not_10_out, and_11_out);
  Subtractor #(.width(4)) subtractor_1 (
    .a(Ponteiro_cabeca_out_6), .b(counter_3_q), .out(subtractor_1_out));  // open: bin, bout
  D_Flip_Flop d_ff_6 (.clk(in_1), .D(and_8_out), .Q(d_ff_6_q));  // open: Qn, preset, en, reset
  \Lista_de_memória  Posicoes_da_cobrinha (
    .Adress(multiplexer_5_out[3:0]), .Writing(multiplexer_5_out[7:4]), .Write_enable(multiplexer_5_out[8]),
    .Reset(multiplexer_5_out[9]), .CLK(in_1), .out_6(Posicoes_da_cobrinha_out_6));
  assign xnor_2_out = ~(Posicoes_da_cobrinha_out_6 ^ calculo_nova_posicao_1_out_3);  // XNOR_Gate xnor_2, 4 bits wide
  assign xnor_3_out = ~(Comida_out_6 ^ calculo_nova_posicao_1_out_3);  // XNOR_Gate xnor_3, 4 bits wide
  assign xnor_4_out = ~(Ponteiro_cauda_out_6 ^ subtractor_1_out);  // XNOR_Gate xnor_4, 4 bits wide
  and and_9 (and_9_out, xnor_2_out[0], xnor_2_out[1], xnor_2_out[2], xnor_2_out[3]);
  Multiplexer #(.width(4)) multiplexer_6 (
    .in0(4'b0110), .in1(4'b1000), .out(multiplexer_6_out), .sel(and_10_out));  // open: en
  and and_10 (and_10_out, xnor_3_out[0], xnor_3_out[1], xnor_3_out[2], xnor_3_out[3]);
  and and_11 (and_11_out, xnor_4_out[0], xnor_4_out[1], xnor_4_out[2], xnor_4_out[3]);
  Random #(.width(4)) random_3 (.clk(in_1), .out(random_3_out));  // open: next, clr
  Multiplexer #(.width(4)) multiplexer_7 (
    .in0(4'b0101), .in1(multiplexer_6_out), .out(multiplexer_7_out), .sel(and_11_out));  // open: en
  Multiplexer #(.select(4), .width(6)) multiplexer_8 (
    .in1(6'b010000), .in6({2'b01, adder_1_out}), .in8({2'b01, adder_1_out}), .out(multiplexer_8_out),
    .sel(\Estado_da_máquina_out_6 ));  // open: in0, in2, in3, in4, in5, in7, in9, in10, in11, in12, in13, in14, in15, en
  Multiplexer #(.width(4)) multiplexer_9 (
    .in0(multiplexer_7_out), .in1(4'b1110), .out(multiplexer_9_out), .sel(and_9_out));  // open: en
  not not_11 (not_11_out, codificador_do_display_1_out_12);
  \Lista_de_memória  \lista_de_memória_2  (
    .Adress(4'b0000), .Writing(random_3_out), .Write_enable(not_11_out), .Reset(1'b0), .CLK(in_1),
    .out_6(\lista_de_memória_2_out_6 ));
  \Lista_de_memória  Ponteiro_cabeca (
    .Adress(4'b0000), .Writing(multiplexer_8_out[3:0]), .Write_enable(multiplexer_8_out[4]),
    .Reset(multiplexer_8_out[5]), .CLK(in_1), .out_6(Ponteiro_cabeca_out_6));
  Multiplexer #(.width(4)) multiplexer_10 (
    .in0(4'b1001), .in1(4'b1010), .out(multiplexer_10_out), .sel(not_11_out));  // open: en
  Adder #(.width(4)) adder_1 (.a(Ponteiro_cabeca_out_6), .b(4'b0001), .out(adder_1_out));  // open: cin, cout
  Multiplexer #(.select(4), .width(6)) multiplexer_11 (
    .in1(6'b010000), .in6({2'b01, adder_2_out}), .out(multiplexer_11_out), .sel(\Estado_da_máquina_out_6 ));  // open: in0, in2, in3, in4, in5, in7, in8, in9, in10, in11, in12, in13, in14, in15, en
  Adder #(.width(4)) adder_2 (.a(Ponteiro_cauda_out_6), .b(4'b0001), .out(adder_2_out));  // open: cin, cout
  \Lista_de_memória  Ponteiro_cauda (
    .Adress(4'b0000), .Writing(multiplexer_11_out[3:0]), .Write_enable(multiplexer_11_out[4]),
    .Reset(multiplexer_11_out[5]), .CLK(in_1), .out_6(Ponteiro_cauda_out_6));
  D_Flip_Flop d_ff_7 (.clk(in_1), .D(counter_2_q[5]), .Q(d_ff_7_q));  // open: Qn, preset, en, reset
  not not_12 (not_12_out, \Estado_da_máquina_out_6 [3]);
  and and_12 (and_12_out[0], counter_2_q[5], not_13_out);
  not not_13 (not_13_out, d_ff_7_q);
  Counter #(.width(1), .max('h1)) counter_4 (
    .Q(counter_4_q), .clk(in_1), .clr(not_14_out));  // open: load, D, count, carry
  not not_14 (not_14_out, and_13_out);
  and and_13 (and_13_out, \Estado_da_máquina_out_6 [0], \Estado_da_máquina_out_6 [1], \Estado_da_máquina_out_6 [2], not_12_out);
  Multiplexer #(.width(4)) multiplexer_12 (
    .in0(4'b0111), .in1(4'b0011), .out(multiplexer_12_out), .sel(counter_4_q));  // open: en
  Multiplexer #(.select(4), .width(6)) multiplexer_13 (
    .in1({2'b01, random_2_out}), .in10({2'b01, \lista_de_memória_2_out_6 }), .out(multiplexer_13_out),
    .sel(\Estado_da_máquina_out_6 ));  // open: in0, in2, in3, in4, in5, in6, in7, in8, in9, in11, in12, in13, in14, in15, en
  \Lista_de_memória  Comida (
    .Adress(4'b0000), .Writing(multiplexer_13_out[3:0]), .Write_enable(multiplexer_13_out[4]),
    .Reset(multiplexer_13_out[5]), .CLK(in_1), .out_6(Comida_out_6));
  Multiplexer #(.width(12)) multiplexer_14 (
    .in0({5'b00001, Comida_out_6, 3'b100}), .in1({5'b00001, Posicoes_da_cobrinha_out_6, 3'b100}),
    .out(multiplexer_14_out), .sel(counter_1_q));  // open: en
  not not_15 (not_15_out, \Estado_da_máquina_out_6 [0]);
  and and_14 (and_14_out, not_15_out, \Estado_da_máquina_out_6 [1], \Estado_da_máquina_out_6 [2], \Estado_da_máquina_out_6 [3]);
  Subtractor #(.width(4)) subtractor_2 (
    .a(Ponteiro_cauda_out_6), .b(4'b0001), .out(subtractor_2_out));  // open: bin, bout
  Multiplexer #(.width(4)) multiplexer_15 (
    .in0(subtractor_2_out), .in1(Ponteiro_cabeca_out_6), .out(multiplexer_15_out), .sel(counter_4_q),
    .en(and_13_out));
  Animacao_morte animacao_morte_1 (
    .in_1(and_14_out), .in_2(in_1), .T(animacao_morte_1_t[0]), .R(animacao_morte_1_t[1]),
    .S(animacao_morte_1_t[2]), .Y(animacao_morte_1_y), .out_7(animacao_morte_1_out_7));
  or or_1 (\input [0], in_3, in_4, in_5, in_6);
  or or_2 (\input [1], in_4, in_6);
  or or_3 (\input [2], in_6, in_5);
  Multiplexer #(.width(4)) multiplexer_16 (
    .in0(4'b1110), .in1(4'b0000), .out(multiplexer_16_out), .sel(animacao_morte_1_out_7));  // open: en
  Multiplexer #(.select(4), .width(12)) multiplexer_17 (
    .in2(multiplexer_14_out), .in3({5'b00001, Comida_out_6, 2'b00, and_12_out[0]}),
    .in7({5'b00001, Posicoes_da_cobrinha_out_6, 3'b001}), .in9({random_3_out, {8{1'b0}}}),
    .in10({5'b00001, \lista_de_memória_2_out_6 , 3'b100}),
    .in14({5'b00001, animacao_morte_1_y, animacao_morte_1_t}), .out(multiplexer_17_out),
    .sel(\Estado_da_máquina_out_6 ));  // open: in0, in1, in4, in5, in6, in8, in11, in12, in13, in15, en
  Codificador_do_display codificador_do_display_1 (
    .X(multiplexer_17_out[6:3]), .CLK(in_1), .\Y₃ (out_7), .\Y₂ (out_8), .\Y₁ (out_9), .\Y₀ (out_10),
    .S(multiplexer_17_out[2]), .R(multiplexer_17_out[1]), .T(multiplexer_17_out[0]),
    .write_enable(multiplexer_17_out[7]), .in_7(multiplexer_17_out[11:8]),
    .out_12(codificador_do_display_1_out_12));
  DotMatrix #(.matrixcols(4), .matrixrows(4)) dotmatrix_1 (
    .col0(undriven), .col1(undriven_2), .col2(undriven_3), .col3(undriven_4));
  // AND_Gate and_15 is placed but not wired
  // AND_Gate and_16 is placed but not wired
endmodule

module FlipFlop_JK_Plus (
  input  in_1,
  input  in_2,
  input  in_3,
  input  in_4,
  output out_5
);

  wire or_1_out, or_2_out;

  or or_1 (or_1_out, in_1, in_4);
  or or_2 (or_2_out, in_4, in_3);
  J_K_Flip_Flop j_k_ff_1 (.J(or_1_out), .clk(in_2), .K(or_2_out), .Q(out_5));  // open: Qn, preset, en, reset
endmodule

module \Memória_do_display  (
  input  \S₁₅ ,
  input  \S₁₄ ,
  input  \S₁₃ ,
  input  \S₁₂ ,
  input  \S₁₁ ,
  input  \S₁₀ ,
  input  \S₉ ,
  input  \S₈ ,
  input  \S₇ ,
  input  \S₆ ,
  input  \S₅ ,
  input  \S₄ ,
  input  \S₃ ,
  input  \S₂ ,
  input  \S₁ ,
  input  \S₀ ,
  input  \R₁₅ ,
  input  \R₁₄ ,
  input  \R₁₃ ,
  input  \R₁₂ ,
  input  \R₁₁ ,
  input  \R₁₀ ,
  input  \R₉ ,
  input  \R₈ ,
  input  \R₇ ,
  input  \R₆ ,
  input  \R₅ ,
  input  \R₄ ,
  input  \R₃ ,
  input  \R₂ ,
  input  \R₁ ,
  input  \R₀ ,
  input  \T₁₅ ,
  input  \T₁₄ ,
  input  \T₁₃ ,
  input  \T₁₂ ,
  input  \T₁₁ ,
  input  \T₁₀ ,
  input  \T₉ ,
  input  \T₈ ,
  input  \T₇ ,
  input  \T₆ ,
  input  \T₅ ,
  input  \T₄ ,
  input  \T₃ ,
  input  \T₂ ,
  input  \T₁ ,
  input  \T₀ ,
  input  CLK,
  input  [3:0] in_50,
  output \Q₁₅ ,
  output \Q₁₄ ,
  output \Q₁₃ ,
  output \Q₁₂ ,
  output \Q₁₁ ,
  output \Q₁₀ ,
  output \Q₉ ,
  output \Q₈ ,
  output \Q₇ ,
  output \Q₆ ,
  output \Q₅ ,
  output \Q₄ ,
  output \Q₃ ,
  output \Q₂ ,
  output \Q₁ ,
  output \Q₀ ,
  output out_67
);

  FlipFlop_JK_Plus flipflop_jk_plus_1 (.in_1(\S₀ ), .out_5(\Q₀ ), .in_3(\R₀ ), .in_4(\T₀ ), .in_2(CLK));
  FlipFlop_JK_Plus flipflop_jk_plus_2 (.in_1(\S₁ ), .out_5(\Q₁ ), .in_3(\R₁ ), .in_4(\T₁ ), .in_2(CLK));
  FlipFlop_JK_Plus flipflop_jk_plus_3 (.in_1(\S₂ ), .out_5(\Q₂ ), .in_3(\R₂ ), .in_4(\T₂ ), .in_2(CLK));
  LED led_1 ();  // open: in
  LED led_2 ();  // open: in
  LED led_3 ();  // open: in
  LED led_4 ();  // open: in
  LED led_5 ();  // open: in
  LED led_6 ();  // open: in
  LED led_7 ();  // open: in
  LED led_8 ();  // open: in
  LED led_9 ();  // open: in
  LED led_10 ();  // open: in
  LED led_11 ();  // open: in
  LED led_12 ();  // open: in
  LED led_13 ();  // open: in
  LED led_14 ();  // open: in
  LED led_15 ();  // open: in
  LED led_16 ();  // open: in
  FlipFlop_JK_Plus flipflop_jk_plus_4 (.in_1(\S₃ ), .out_5(\Q₃ ), .in_3(\R₃ ), .in_4(\T₃ ), .in_2(CLK));
  FlipFlop_JK_Plus flipflop_jk_plus_5 (.in_1(\S₄ ), .out_5(\Q₄ ), .in_3(\R₄ ), .in_4(\T₄ ), .in_2(CLK));
  FlipFlop_JK_Plus flipflop_jk_plus_6 (.in_1(\S₅ ), .out_5(\Q₅ ), .in_3(\R₅ ), .in_4(\T₅ ), .in_2(CLK));
  FlipFlop_JK_Plus flipflop_jk_plus_7 (.in_1(\S₆ ), .out_5(\Q₆ ), .in_3(\R₆ ), .in_4(\T₆ ), .in_2(CLK));
  FlipFlop_JK_Plus flipflop_jk_plus_8 (.in_1(\S₇ ), .out_5(\Q₇ ), .in_3(\R₇ ), .in_4(\T₇ ), .in_2(CLK));
  FlipFlop_JK_Plus flipflop_jk_plus_9 (.in_1(\S₈ ), .out_5(\Q₈ ), .in_3(\R₈ ), .in_4(\T₈ ), .in_2(CLK));
  FlipFlop_JK_Plus flipflop_jk_plus_10 (.in_1(\S₉ ), .out_5(\Q₉ ), .in_3(\R₉ ), .in_4(\T₉ ), .in_2(CLK));
  FlipFlop_JK_Plus flipflop_jk_plus_11 (.in_1(\S₁₀ ), .out_5(\Q₁₀ ), .in_3(\R₁₀ ), .in_4(\T₁₀ ), .in_2(CLK));
  FlipFlop_JK_Plus flipflop_jk_plus_12 (.in_1(\S₁₁ ), .out_5(\Q₁₁ ), .in_3(\R₁₁ ), .in_4(\T₁₁ ), .in_2(CLK));
  FlipFlop_JK_Plus flipflop_jk_plus_13 (.in_1(\S₁₂ ), .out_5(\Q₁₂ ), .in_3(\R₁₂ ), .in_4(\T₁₂ ), .in_2(CLK));
  FlipFlop_JK_Plus flipflop_jk_plus_14 (.in_1(\S₁₃ ), .out_5(\Q₁₃ ), .in_3(\R₁₃ ), .in_4(\T₁₃ ), .in_2(CLK));
  FlipFlop_JK_Plus flipflop_jk_plus_15 (.in_1(\S₁₄ ), .out_5(\Q₁₄ ), .in_3(\R₁₄ ), .in_4(\T₁₄ ), .in_2(CLK));
  FlipFlop_JK_Plus flipflop_jk_plus_16 (.in_1(\S₁₅ ), .out_5(\Q₁₅ ), .in_3(\R₁₅ ), .in_4(\T₁₅ ), .in_2(CLK));
  Multiplexer #(.select(4)) multiplexer_1 (
    .in0(\Q₀ ), .in1(\Q₁ ), .in2(\Q₂ ), .in3(\Q₃ ), .in4(\Q₄ ), .in5(\Q₅ ), .in6(\Q₆ ), .in7(\Q₇ ),
    .in8(\Q₈ ), .in9(\Q₉ ), .in10(\Q₁₀ ), .in11(\Q₁₁ ), .in12(\Q₁₂ ), .in13(\Q₁₃ ), .in14(\Q₁₄ ),
    .in15(\Q₁₅ ), .out(out_67), .sel(in_50));  // open: en
endmodule

module Codificador_do_display (
  input  write_enable,
  input  S,
  input  R,
  input  T,
  input  [3:0] X,
  input  CLK,
  input  [3:0] in_7,
  output [3:0] \Y₃ ,
  output [3:0] \Y₂ ,
  output [3:0] \Y₁ ,
  output [3:0] \Y₀ ,
  output out_12
);

  wire and_1_out, and_2_out, and_3_out, and_4_out, and_5_out, and_6_out, and_7_out, and_8_out, and_9_out,
       and_10_out, and_11_out, and_12_out, and_13_out, and_14_out, and_15_out, and_16_out, and_17_out,
       and_18_out, and_19_out, and_20_out, and_21_out, and_22_out, and_23_out, and_24_out, and_25_out,
       and_26_out, and_27_out, and_28_out, and_29_out, and_30_out, and_31_out, and_32_out, and_33_out,
       and_34_out, and_35_out, and_36_out, and_37_out, and_38_out, and_39_out, and_40_out, and_41_out,
       and_42_out, and_43_out, and_44_out, and_45_out, and_46_out, and_47_out, and_48_out, and_49_out,
       and_50_out, and_51_out, decoder_1_out0, decoder_1_out1, decoder_1_out2, decoder_1_out3,
       decoder_1_out4, decoder_1_out5, decoder_1_out6, decoder_1_out7, decoder_1_out8, decoder_1_out9,
       decoder_1_out10, decoder_1_out11, decoder_1_out12, decoder_1_out13, decoder_1_out14, decoder_1_out15;

  Decoder #(.select(4)) decoder_1 (
    .out0(decoder_1_out0), .out1(decoder_1_out1), .out2(decoder_1_out2), .out3(decoder_1_out3),
    .out4(decoder_1_out4), .out5(decoder_1_out5), .out6(decoder_1_out6), .out7(decoder_1_out7),
    .out8(decoder_1_out8), .out9(decoder_1_out9), .out10(decoder_1_out10), .out11(decoder_1_out11),
    .out12(decoder_1_out12), .out13(decoder_1_out13), .out14(decoder_1_out14), .out15(decoder_1_out15),
    .sel(X));  // open: en
  and and_1 (and_1_out, write_enable, S);
  and and_2 (and_2_out, write_enable, R);
  and and_3 (and_3_out, write_enable, T);
  and and_4 (and_4_out, and_3_out, decoder_1_out0);
  and and_5 (and_5_out, and_3_out, decoder_1_out1);
  and and_6 (and_6_out, and_3_out, decoder_1_out2);
  and and_7 (and_7_out, and_3_out, decoder_1_out3);
  and and_8 (and_8_out, and_3_out, decoder_1_out4);
  and and_9 (and_9_out, and_3_out, decoder_1_out5);
  and and_10 (and_10_out, and_3_out, decoder_1_out6);
  and and_11 (and_11_out, and_3_out, decoder_1_out7);
  and and_12 (and_12_out, and_3_out, decoder_1_out8);
  and and_13 (and_13_out, and_3_out, decoder_1_out9);
  and and_14 (and_14_out, and_3_out, decoder_1_out10);
  and and_15 (and_15_out, and_3_out, decoder_1_out11);
  and and_16 (and_16_out, and_3_out, decoder_1_out12);
  and and_17 (and_17_out, and_3_out, decoder_1_out13);
  and and_18 (and_18_out, and_3_out, decoder_1_out14);
  and and_19 (and_19_out, and_3_out, decoder_1_out15);
  and and_20 (and_20_out, and_1_out, decoder_1_out0);
  and and_21 (and_21_out, and_2_out, decoder_1_out0);
  and and_22 (and_22_out, and_1_out, decoder_1_out1);
  and and_23 (and_23_out, and_2_out, decoder_1_out1);
  and and_24 (and_24_out, and_1_out, decoder_1_out2);
  and and_25 (and_25_out, and_2_out, decoder_1_out2);
  and and_26 (and_26_out, and_1_out, decoder_1_out3);
  and and_27 (and_27_out, and_2_out, decoder_1_out3);
  and and_28 (and_28_out, and_1_out, decoder_1_out4);
  and and_29 (and_29_out, and_2_out, decoder_1_out4);
  and and_30 (and_30_out, and_1_out, decoder_1_out5);
  and and_31 (and_31_out, and_2_out, decoder_1_out5);
  and and_32 (and_32_out, and_1_out, decoder_1_out6);
  and and_33 (and_33_out, and_2_out, decoder_1_out6);
  and and_34 (and_34_out, and_1_out, decoder_1_out7);
  and and_35 (and_35_out, and_2_out, decoder_1_out7);
  and and_36 (and_36_out, and_1_out, decoder_1_out8);
  and and_37 (and_37_out, and_2_out, decoder_1_out8);
  and and_38 (and_38_out, and_1_out, decoder_1_out9);
  and and_39 (and_39_out, and_2_out, decoder_1_out9);
  and and_40 (and_40_out, and_1_out, decoder_1_out10);
  and and_41 (and_41_out, and_2_out, decoder_1_out10);
  and and_42 (and_42_out, and_1_out, decoder_1_out11);
  and and_43 (and_43_out, and_2_out, decoder_1_out11);
  and and_44 (and_44_out, and_1_out, decoder_1_out12);
  and and_45 (and_45_out, and_2_out, decoder_1_out12);
  and and_46 (and_46_out, and_1_out, decoder_1_out13);
  and and_47 (and_47_out, and_2_out, decoder_1_out13);
  and and_48 (and_48_out, and_1_out, decoder_1_out14);
  and and_49 (and_49_out, and_2_out, decoder_1_out14);
  and and_50 (and_50_out, and_1_out, decoder_1_out15);
  and and_51 (and_51_out, and_2_out, decoder_1_out15);
  \Memória_do_display  \memória_do_display_1  (
    .\S₁₅ (and_50_out), .\S₁₄ (and_48_out), .\S₁₃ (and_46_out), .\S₁₂ (and_44_out), .\S₁₁ (and_42_out),
    .\S₁₀ (and_40_out), .\S₉ (and_38_out), .\S₈ (and_36_out), .\S₇ (and_34_out), .\S₆ (and_32_out),
    .\S₅ (and_30_out), .\S₄ (and_28_out), .\S₃ (and_26_out), .\S₂ (and_24_out), .\S₁ (and_22_out),
    .\S₀ (and_20_out), .\R₁₅ (and_51_out), .\R₁₄ (and_49_out), .\R₁₃ (and_47_out), .\R₁₂ (and_45_out),
    .\R₁₁ (and_43_out), .\R₁₀ (and_41_out), .\R₉ (and_39_out), .\R₈ (and_37_out), .\R₇ (and_35_out),
    .\R₆ (and_33_out), .\R₅ (and_31_out), .\R₄ (and_29_out), .\R₃ (and_27_out), .\R₂ (and_25_out),
    .\R₁ (and_23_out), .\R₀ (and_21_out), .\T₁₅ (and_19_out), .\T₁₄ (and_18_out), .\T₁₃ (and_17_out),
    .\T₁₂ (and_16_out), .\T₁₁ (and_15_out), .\T₁₀ (and_14_out), .\T₉ (and_13_out), .\T₈ (and_12_out),
    .\T₇ (and_11_out), .\T₆ (and_10_out), .\T₅ (and_9_out), .\T₄ (and_8_out), .\T₃ (and_7_out),
    .\T₂ (and_6_out), .\T₁ (and_5_out), .\T₀ (and_4_out), .CLK(CLK), .\Q₁₅ (\Y₃ [0]), .\Q₁₄ (\Y₂ [0]),
    .\Q₁₃ (\Y₁ [0]), .\Q₁₂ (\Y₀ [0]), .\Q₁₁ (\Y₃ [1]), .\Q₁₀ (\Y₂ [1]), .\Q₉ (\Y₁ [1]), .\Q₈ (\Y₀ [1]),
    .\Q₇ (\Y₃ [2]), .\Q₆ (\Y₂ [2]), .\Q₅ (\Y₁ [2]), .\Q₄ (\Y₀ [2]), .\Q₃ (\Y₃ [3]), .\Q₂ (\Y₂ [3]),
    .\Q₁ (\Y₁ [3]), .\Q₀ (\Y₀ [3]), .in_50(in_7), .out_67(out_12));
  Decoder decoder_2 ();  // open: out0, out1, sel, en
endmodule

module \Lista_de_memória  (
  input  [3:0] Adress,
  input  [3:0] Writing,
  input  Write_enable,
  input  Reset,
  input  CLK,
  output [3:0] out_6
);

  wire and_1_out, and_2_out, and_3_out, and_4_out, and_5_out, and_6_out, and_7_out, and_8_out, and_9_out,
       and_10_out, and_11_out, and_12_out, and_13_out, and_14_out, and_15_out, and_16_out, and_17_out,
       and_18_out, and_19_out, and_20_out, and_21_out, and_22_out, and_23_out, and_24_out, and_25_out,
       and_26_out, and_27_out, and_28_out, and_29_out, and_30_out, and_31_out, and_32_out, and_33_out,
       and_34_out, and_35_out, and_36_out, and_37_out, and_38_out, and_39_out, and_40_out, and_41_out,
       and_42_out, and_43_out, and_44_out, and_45_out, and_46_out, and_47_out, and_48_out, and_49_out,
       and_50_out, and_51_out, and_52_out, and_53_out, and_54_out, and_55_out, and_56_out, and_57_out,
       and_58_out, and_59_out, and_60_out, and_61_out, and_62_out, and_63_out, and_64_out, and_65_out,
       and_66_out, and_67_out, and_68_out, and_69_out, and_70_out, and_71_out, and_72_out, and_73_out,
       and_74_out, and_75_out, and_76_out, and_77_out, and_78_out, and_79_out, and_80_out, and_81_out,
       and_82_out, and_83_out, and_84_out, and_85_out, and_86_out, and_87_out, and_88_out, and_89_out,
       and_90_out, and_91_out, and_92_out, and_93_out, and_94_out, and_95_out, and_96_out, and_97_out,
       and_98_out, and_99_out, and_100_out, and_101_out, and_102_out, and_103_out, and_104_out, and_105_out,
       and_106_out, and_107_out, and_108_out, and_109_out, and_110_out, and_111_out, and_112_out,
       and_113_out, and_114_out, and_115_out, and_116_out, and_117_out, and_118_out, and_119_out,
       and_120_out, and_121_out, and_122_out, and_123_out, and_124_out, and_125_out, and_126_out,
       and_127_out, and_128_out, decoder_1_out0, decoder_1_out1, decoder_1_out2, decoder_1_out3,
       decoder_1_out4, decoder_1_out5, decoder_1_out6, decoder_1_out7, decoder_1_out8, decoder_1_out9,
       decoder_1_out10, decoder_1_out11, decoder_1_out12, decoder_1_out13, decoder_1_out14, decoder_1_out15,
       not_1_out, not_2_out, not_3_out, not_4_out, not_5_out, not_6_out, not_7_out, not_8_out, not_9_out,
       not_10_out, not_11_out, not_12_out, not_13_out, not_14_out, not_15_out, not_16_out, not_17_out,
       not_18_out, not_19_out, not_20_out, not_21_out, not_22_out, not_23_out, not_24_out, not_25_out,
       not_26_out, not_27_out, not_28_out, not_29_out, not_30_out, not_31_out, not_32_out, not_33_out,
       not_34_out, not_35_out, not_36_out, not_37_out, not_38_out, not_39_out, not_40_out, not_41_out,
       not_42_out, not_43_out, not_44_out, not_45_out, not_46_out, not_47_out, not_48_out, not_49_out,
       not_50_out, not_51_out, not_52_out, not_53_out, not_54_out, not_55_out, not_56_out, not_57_out,
       not_58_out, not_59_out, not_60_out, not_61_out, not_62_out, not_63_out, not_64_out, or_1_out,
       or_2_out, or_3_out, or_4_out, or_5_out, or_6_out, or_7_out, or_8_out, or_9_out, or_10_out, or_11_out,
       or_12_out, or_13_out, or_14_out, or_15_out, or_16_out, or_17_out, or_18_out, or_19_out, or_20_out,
       or_21_out, or_22_out, or_23_out, or_24_out, or_25_out, or_26_out, or_27_out, or_28_out, or_29_out,
       or_30_out, or_31_out, or_32_out, or_33_out, or_34_out, or_35_out, or_36_out, or_37_out, or_38_out,
       or_39_out, or_40_out, or_41_out, or_42_out, or_43_out, or_44_out, or_45_out, or_46_out, or_47_out,
       or_48_out, or_49_out, or_50_out, or_51_out, or_52_out, or_53_out, or_54_out, or_55_out, or_56_out,
       or_57_out, or_58_out, or_59_out, or_60_out, or_61_out, or_62_out, or_63_out, or_64_out;
  wire [3:0] flipflop_jk_plus_13_out_5, flipflop_jk_plus_14_out_5, flipflop_jk_plus_15_out_5,
       flipflop_jk_plus_16_out_5, flipflop_jk_plus_29_out_5, flipflop_jk_plus_30_out_5,
       flipflop_jk_plus_31_out_5, flipflop_jk_plus_32_out_5, flipflop_jk_plus_45_out_5,
       flipflop_jk_plus_46_out_5, flipflop_jk_plus_47_out_5, flipflop_jk_plus_48_out_5,
       flipflop_jk_plus_61_out_5, flipflop_jk_plus_62_out_5, flipflop_jk_plus_63_out_5,
       flipflop_jk_plus_64_out_5, multiplexer_1_out;

  Multiplexer #(.width(4)) multiplexer_1 (
    .in0(Writing), .in1(4'b0000), .out(multiplexer_1_out), .sel(Reset));  // open: en
  Decoder #(.select(4)) decoder_1 (
    .out0(decoder_1_out0), .out1(decoder_1_out1), .out2(decoder_1_out2), .out3(decoder_1_out3),
    .out4(decoder_1_out4), .out5(decoder_1_out5), .out6(decoder_1_out6), .out7(decoder_1_out7),
    .out8(decoder_1_out8), .out9(decoder_1_out9), .out10(decoder_1_out10), .out11(decoder_1_out11),
    .out12(decoder_1_out12), .out13(decoder_1_out13), .out14(decoder_1_out14), .out15(decoder_1_out15),
    .sel(Adress), .en(Write_enable));
  and and_1 (and_1_out, multiplexer_1_out[0], decoder_1_out0);
  and and_2 (and_2_out, multiplexer_1_out[1], decoder_1_out0);
  and and_3 (and_3_out, multiplexer_1_out[2], decoder_1_out0);
  and and_4 (and_4_out, multiplexer_1_out[3], decoder_1_out0);
  not not_1 (not_1_out, multiplexer_1_out[0]);
  and and_5 (and_5_out, not_1_out, decoder_1_out0);
  not not_2 (not_2_out, multiplexer_1_out[1]);
  and and_6 (and_6_out, not_2_out, decoder_1_out0);
  not not_3 (not_3_out, multiplexer_1_out[2]);
  and and_7 (and_7_out, not_3_out, decoder_1_out0);
  not not_4 (not_4_out, multiplexer_1_out[3]);
  and and_8 (and_8_out, not_4_out, decoder_1_out0);
  FlipFlop_JK_Plus flipflop_jk_plus_1 (
    .in_1(and_4_out), .out_5(flipflop_jk_plus_13_out_5[3]), .in_3(or_2_out), .in_4(1'b0), .in_2(CLK));
  and and_9 (and_9_out, multiplexer_1_out[0], decoder_1_out4);
  and and_10 (and_10_out, multiplexer_1_out[1], decoder_1_out4);
  and and_11 (and_11_out, multiplexer_1_out[2], decoder_1_out4);
  and and_12 (and_12_out, multiplexer_1_out[3], decoder_1_out4);
  not not_5 (not_5_out, multiplexer_1_out[0]);
  and and_13 (and_13_out, not_5_out, decoder_1_out4);
  not not_6 (not_6_out, multiplexer_1_out[1]);
  and and_14 (and_14_out, not_6_out, decoder_1_out4);
  not not_7 (not_7_out, multiplexer_1_out[2]);
  and and_15 (and_15_out, not_7_out, decoder_1_out4);
  not not_8 (not_8_out, multiplexer_1_out[3]);
  and and_16 (and_16_out, not_8_out, decoder_1_out4);
  FlipFlop_JK_Plus flipflop_jk_plus_2 (
    .in_1(and_12_out), .out_5(flipflop_jk_plus_14_out_5[3]), .in_3(or_4_out), .in_4(1'b0), .in_2(CLK));
  and and_17 (and_17_out, multiplexer_1_out[0], decoder_1_out8);
  and and_18 (and_18_out, multiplexer_1_out[1], decoder_1_out8);
  and and_19 (and_19_out, multiplexer_1_out[2], decoder_1_out8);
  and and_20 (and_20_out, multiplexer_1_out[3], decoder_1_out8);
  not not_9 (not_9_out, multiplexer_1_out[0]);
  and and_21 (and_21_out, not_9_out, decoder_1_out8);
  not not_10 (not_10_out, multiplexer_1_out[1]);
  and and_22 (and_22_out, not_10_out, decoder_1_out8);
  not not_11 (not_11_out, multiplexer_1_out[2]);
  and and_23 (and_23_out, not_11_out, decoder_1_out8);
  not not_12 (not_12_out, multiplexer_1_out[3]);
  and and_24 (and_24_out, not_12_out, decoder_1_out8);
  FlipFlop_JK_Plus flipflop_jk_plus_3 (
    .in_1(and_20_out), .out_5(flipflop_jk_plus_15_out_5[3]), .in_3(or_6_out), .in_4(1'b0), .in_2(CLK));
  and and_25 (and_25_out, multiplexer_1_out[0], decoder_1_out12);
  and and_26 (and_26_out, multiplexer_1_out[1], decoder_1_out12);
  and and_27 (and_27_out, multiplexer_1_out[2], decoder_1_out12);
  and and_28 (and_28_out, multiplexer_1_out[3], decoder_1_out12);
  not not_13 (not_13_out, multiplexer_1_out[0]);
  and and_29 (and_29_out, not_13_out, decoder_1_out12);
  not not_14 (not_14_out, multiplexer_1_out[1]);
  and and_30 (and_30_out, not_14_out, decoder_1_out12);
  not not_15 (not_15_out, multiplexer_1_out[2]);
  and and_31 (and_31_out, not_15_out, decoder_1_out12);
  not not_16 (not_16_out, multiplexer_1_out[3]);
  and and_32 (and_32_out, not_16_out, decoder_1_out12);
  FlipFlop_JK_Plus flipflop_jk_plus_4 (
    .in_1(and_28_out), .out_5(flipflop_jk_plus_16_out_5[3]), .in_3(or_8_out), .in_4(1'b0), .in_2(CLK));
  or or_1 (or_1_out, Reset, and_7_out);
  or or_2 (or_2_out, Reset, and_8_out);
  FlipFlop_JK_Plus flipflop_jk_plus_5 (
    .in_1(and_3_out), .out_5(flipflop_jk_plus_13_out_5[2]), .in_3(or_1_out), .in_4(1'b0), .in_2(CLK));
  or or_3 (or_3_out, Reset, and_15_out);
  or or_4 (or_4_out, Reset, and_16_out);
  FlipFlop_JK_Plus flipflop_jk_plus_6 (
    .in_1(and_11_out), .out_5(flipflop_jk_plus_14_out_5[2]), .in_3(or_3_out), .in_4(1'b0), .in_2(CLK));
  or or_5 (or_5_out, Reset, and_23_out);
  or or_6 (or_6_out, Reset, and_24_out);
  FlipFlop_JK_Plus flipflop_jk_plus_7 (
    .in_1(and_19_out), .out_5(flipflop_jk_plus_15_out_5[2]), .in_3(or_5_out), .in_4(1'b0), .in_2(CLK));
  or or_7 (or_7_out, Reset, and_31_out);
  or or_8 (or_8_out, Reset, and_32_out);
  FlipFlop_JK_Plus flipflop_jk_plus_8 (
    .in_1(and_27_out), .out_5(flipflop_jk_plus_16_out_5[2]), .in_3(or_7_out), .in_4(1'b0), .in_2(CLK));
  or or_9 (or_9_out, Reset, and_6_out);
  or or_10 (or_10_out, Reset, and_14_out);
  or or_11 (or_11_out, Reset, and_22_out);
  or or_12 (or_12_out, Reset, and_30_out);
  or or_13 (or_13_out, Reset, and_5_out);
  FlipFlop_JK_Plus flipflop_jk_plus_9 (
    .in_1(and_2_out), .out_5(flipflop_jk_plus_13_out_5[1]), .in_3(or_9_out), .in_4(1'b0), .in_2(CLK));
  or or_14 (or_14_out, Reset, and_13_out);
  FlipFlop_JK_Plus flipflop_jk_plus_10 (
    .in_1(and_10_out), .out_5(flipflop_jk_plus_14_out_5[1]), .in_3(or_10_out), .in_4(1'b0), .in_2(CLK));
  or or_15 (or_15_out, Reset, and_21_out);
  FlipFlop_JK_Plus flipflop_jk_plus_11 (
    .in_1(and_18_out), .out_5(flipflop_jk_plus_15_out_5[1]), .in_3(or_11_out), .in_4(1'b0), .in_2(CLK));
  or or_16 (or_16_out, Reset, and_29_out);
  FlipFlop_JK_Plus flipflop_jk_plus_12 (
    .in_1(and_26_out), .out_5(flipflop_jk_plus_16_out_5[1]), .in_3(or_12_out), .in_4(1'b0), .in_2(CLK));
  FlipFlop_JK_Plus flipflop_jk_plus_13 (
    .in_1(and_1_out), .out_5(flipflop_jk_plus_13_out_5[0]), .in_3(or_13_out), .in_4(1'b0), .in_2(CLK));
  FlipFlop_JK_Plus flipflop_jk_plus_14 (
    .in_1(and_9_out), .out_5(flipflop_jk_plus_14_out_5[0]), .in_3(or_14_out), .in_4(1'b0), .in_2(CLK));
  FlipFlop_JK_Plus flipflop_jk_plus_15 (
    .in_1(and_17_out), .out_5(flipflop_jk_plus_15_out_5[0]), .in_3(or_15_out), .in_4(1'b0), .in_2(CLK));
  FlipFlop_JK_Plus flipflop_jk_plus_16 (
    .in_1(and_25_out), .out_5(flipflop_jk_plus_16_out_5[0]), .in_3(or_16_out), .in_4(1'b0), .in_2(CLK));
  and and_33 (and_33_out, multiplexer_1_out[0], decoder_1_out1);
  and and_34 (and_34_out, multiplexer_1_out[1], decoder_1_out1);
  and and_35 (and_35_out, multiplexer_1_out[2], decoder_1_out1);
  and and_36 (and_36_out, multiplexer_1_out[3], decoder_1_out1);
  not not_17 (not_17_out, multiplexer_1_out[0]);
  and and_37 (and_37_out, not_17_out, decoder_1_out1);
  not not_18 (not_18_out, multiplexer_1_out[1]);
  and and_38 (and_38_out, not_18_out, decoder_1_out1);
  not not_19 (not_19_out, multiplexer_1_out[2]);
  and and_39 (and_39_out, not_19_out, decoder_1_out1);
  not not_20 (not_20_out, multiplexer_1_out[3]);
  and and_40 (and_40_out, not_20_out, decoder_1_out1);
  and and_41 (and_41_out, multiplexer_1_out[0], decoder_1_out5);
  and and_42 (and_42_out, multiplexer_1_out[1], decoder_1_out5);
  and and_43 (and_43_out, multiplexer_1_out[2], decoder_1_out5);
  and and_44 (and_44_out, multiplexer_1_out[3], decoder_1_out5);
  not not_21 (not_21_out, multiplexer_1_out[0]);
  and and_45 (and_45_out, not_21_out, decoder_1_out5);
  not not_22 (not_22_out, multiplexer_1_out[1]);
  and and_46 (and_46_out, not_22_out, decoder_1_out5);
  not not_23 (not_23_out, multiplexer_1_out[2]);
  and and_47 (and_47_out, not_23_out, decoder_1_out5);
  not not_24 (not_24_out, multiplexer_1_out[3]);
  and and_48 (and_48_out, not_24_out, decoder_1_out5);
  and and_49 (and_49_out, multiplexer_1_out[0], decoder_1_out9);
  and and_50 (and_50_out, multiplexer_1_out[1], decoder_1_out9);
  and and_51 (and_51_out, multiplexer_1_out[2], decoder_1_out9);
  and and_52 (and_52_out, multiplexer_1_out[3], decoder_1_out9);
  not not_25 (not_25_out, multiplexer_1_out[0]);
  and and_53 (and_53_out, not_25_out, decoder_1_out9);
  not not_26 (not_26_out, multiplexer_1_out[1]);
  and and_54 (and_54_out, not_26_out, decoder_1_out9);
  not not_27 (not_27_out, multiplexer_1_out[2]);
  and and_55 (and_55_out, not_27_out, decoder_1_out9);
  not not_28 (not_28_out, multiplexer_1_out[3]);
  and and_56 (and_56_out, not_28_out, decoder_1_out9);
  and and_57 (and_57_out, multiplexer_1_out[0], decoder_1_out13);
  and and_58 (and_58_out, multiplexer_1_out[1], decoder_1_out13);
  and and_59 (and_59_out, multiplexer_1_out[2], decoder_1_out13);
  and and_60 (and_60_out, multiplexer_1_out[3], decoder_1_out13);
  not not_29 (not_29_out, multiplexer_1_out[0]);
  and and_61 (and_61_out, not_29_out, decoder_1_out13);
  not not_30 (not_30_out, multiplexer_1_out[1]);
  and and_62 (and_62_out, not_30_out, decoder_1_out13);
  not not_31 (not_31_out, multiplexer_1_out[2]);
  and and_63 (and_63_out, not_31_out, decoder_1_out13);
  not not_32 (not_32_out, multiplexer_1_out[3]);
  and and_64 (and_64_out, not_32_out, decoder_1_out13);
  or or_17 (or_17_out, Reset, and_39_out);
  or or_18 (or_18_out, Reset, and_40_out);
  FlipFlop_JK_Plus flipflop_jk_plus_17 (
    .in_1(and_36_out), .out_5(flipflop_jk_plus_29_out_5[3]), .in_3(or_18_out), .in_4(1'b0), .in_2(CLK));
  or or_19 (or_19_out, Reset, and_47_out);
  or or_20 (or_20_out, Reset, and_48_out);
  FlipFlop_JK_Plus flipflop_jk_plus_18 (
    .in_1(and_44_out), .out_5(flipflop_jk_plus_30_out_5[3]), .in_3(or_20_out), .in_4(1'b0), .in_2(CLK));
  or or_21 (or_21_out, Reset, and_55_out);
  or or_22 (or_22_out, Reset, and_56_out);
  FlipFlop_JK_Plus flipflop_jk_plus_19 (
    .in_1(and_52_out), .out_5(flipflop_jk_plus_31_out_5[3]), .in_3(or_22_out), .in_4(1'b0), .in_2(CLK));
  or or_23 (or_23_out, Reset, and_63_out);
  or or_24 (or_24_out, Reset, and_64_out);
  FlipFlop_JK_Plus flipflop_jk_plus_20 (
    .in_1(and_60_out), .out_5(flipflop_jk_plus_32_out_5[3]), .in_3(or_24_out), .in_4(1'b0), .in_2(CLK));
  or or_25 (or_25_out, Reset, and_38_out);
  FlipFlop_JK_Plus flipflop_jk_plus_21 (
    .in_1(and_35_out), .out_5(flipflop_jk_plus_29_out_5[2]), .in_3(or_17_out), .in_4(1'b0), .in_2(CLK));
  FlipFlop_JK_Plus flipflop_jk_plus_22 (
    .in_1(and_43_out), .out_5(flipflop_jk_plus_30_out_5[2]), .in_3(or_19_out), .in_4(1'b0), .in_2(CLK));
  FlipFlop_JK_Plus flipflop_jk_plus_23 (
    .in_1(and_51_out), .out_5(flipflop_jk_plus_31_out_5[2]), .in_3(or_21_out), .in_4(1'b0), .in_2(CLK));
  FlipFlop_JK_Plus flipflop_jk_plus_24 (
    .in_1(and_59_out), .out_5(flipflop_jk_plus_32_out_5[2]), .in_3(or_23_out), .in_4(1'b0), .in_2(CLK));
  FlipFlop_JK_Plus flipflop_jk_plus_25 (
    .in_1(and_34_out), .out_5(flipflop_jk_plus_29_out_5[1]), .in_3(or_25_out), .in_4(1'b0), .in_2(CLK));
  or or_26 (or_26_out, Reset, and_46_out);
  FlipFlop_JK_Plus flipflop_jk_plus_26 (
    .in_1(and_42_out), .out_5(flipflop_jk_plus_30_out_5[1]), .in_3(or_26_out), .in_4(1'b0), .in_2(CLK));
  or or_27 (or_27_out, Reset, and_54_out);
  FlipFlop_JK_Plus flipflop_jk_plus_27 (
    .in_1(and_50_out), .out_5(flipflop_jk_plus_31_out_5[1]), .in_3(or_27_out), .in_4(1'b0), .in_2(CLK));
  or or_28 (or_28_out, Reset, and_62_out);
  FlipFlop_JK_Plus flipflop_jk_plus_28 (
    .in_1(and_58_out), .out_5(flipflop_jk_plus_32_out_5[1]), .in_3(or_28_out), .in_4(1'b0), .in_2(CLK));
  or or_29 (or_29_out, Reset, and_37_out);
  FlipFlop_JK_Plus flipflop_jk_plus_29 (
    .in_1(and_33_out), .out_5(flipflop_jk_plus_29_out_5[0]), .in_3(or_29_out), .in_4(1'b0), .in_2(CLK));
  or or_30 (or_30_out, Reset, and_45_out);
  FlipFlop_JK_Plus flipflop_jk_plus_30 (
    .in_1(and_41_out), .out_5(flipflop_jk_plus_30_out_5[0]), .in_3(or_30_out), .in_4(1'b0), .in_2(CLK));
  or or_31 (or_31_out, Reset, and_53_out);
  FlipFlop_JK_Plus flipflop_jk_plus_31 (
    .in_1(and_49_out), .out_5(flipflop_jk_plus_31_out_5[0]), .in_3(or_31_out), .in_4(1'b0), .in_2(CLK));
  or or_32 (or_32_out, Reset, and_61_out);
  FlipFlop_JK_Plus flipflop_jk_plus_32 (
    .in_1(and_57_out), .out_5(flipflop_jk_plus_32_out_5[0]), .in_3(or_32_out), .in_4(1'b0), .in_2(CLK));
  and and_65 (and_65_out, multiplexer_1_out[0], decoder_1_out2);
  and and_66 (and_66_out, multiplexer_1_out[1], decoder_1_out2);
  and and_67 (and_67_out, multiplexer_1_out[2], decoder_1_out2);
  and and_68 (and_68_out, multiplexer_1_out[3], decoder_1_out2);
  not not_33 (not_33_out, multiplexer_1_out[0]);
  and and_69 (and_69_out, not_33_out, decoder_1_out2);
  not not_34 (not_34_out, multiplexer_1_out[1]);
  and and_70 (and_70_out, not_34_out, decoder_1_out2);
  not not_35 (not_35_out, multiplexer_1_out[2]);
  and and_71 (and_71_out, not_35_out, decoder_1_out2);
  not not_36 (not_36_out, multiplexer_1_out[3]);
  and and_72 (and_72_out, not_36_out, decoder_1_out2);
  FlipFlop_JK_Plus flipflop_jk_plus_33 (
    .in_1(and_68_out), .out_5(flipflop_jk_plus_45_out_5[3]), .in_3(or_34_out), .in_4(1'b0), .in_2(CLK));
  and and_73 (and_73_out, multiplexer_1_out[0], decoder_1_out6);
  and and_74 (and_74_out, multiplexer_1_out[1], decoder_1_out6);
  and and_75 (and_75_out, multiplexer_1_out[2], decoder_1_out6);
  and and_76 (and_76_out, multiplexer_1_out[3], decoder_1_out6);
  not not_37 (not_37_out, multiplexer_1_out[0]);
  and and_77 (and_77_out, not_37_out, decoder_1_out6);
  not not_38 (not_38_out, multiplexer_1_out[1]);
  and and_78 (and_78_out, not_38_out, decoder_1_out6);
  not not_39 (not_39_out, multiplexer_1_out[2]);
  and and_79 (and_79_out, not_39_out, decoder_1_out6);
  not not_40 (not_40_out, multiplexer_1_out[3]);
  and and_80 (and_80_out, not_40_out, decoder_1_out6);
  FlipFlop_JK_Plus flipflop_jk_plus_34 (
    .in_1(and_76_out), .out_5(flipflop_jk_plus_46_out_5[3]), .in_3(or_36_out), .in_4(1'b0), .in_2(CLK));
  and and_81 (and_81_out, multiplexer_1_out[0], decoder_1_out10);
  and and_82 (and_82_out, multiplexer_1_out[1], decoder_1_out10);
  and and_83 (and_83_out, multiplexer_1_out[2], decoder_1_out10);
  and and_84 (and_84_out, multiplexer_1_out[3], decoder_1_out10);
  not not_41 (not_41_out, multiplexer_1_out[0]);
  and and_85 (and_85_out, not_41_out, decoder_1_out10);
  not not_42 (not_42_out, multiplexer_1_out[1]);
  and and_86 (and_86_out, not_42_out, decoder_1_out10);
  not not_43 (not_43_out, multiplexer_1_out[2]);
  and and_87 (and_87_out, not_43_out, decoder_1_out10);
  not not_44 (not_44_out, multiplexer_1_out[3]);
  and and_88 (and_88_out, not_44_out, decoder_1_out10);
  FlipFlop_JK_Plus flipflop_jk_plus_35 (
    .in_1(and_84_out), .out_5(flipflop_jk_plus_47_out_5[3]), .in_3(or_38_out), .in_4(1'b0), .in_2(CLK));
  and and_89 (and_89_out, multiplexer_1_out[0], decoder_1_out14);
  and and_90 (and_90_out, multiplexer_1_out[1], decoder_1_out14);
  and and_91 (and_91_out, multiplexer_1_out[2], decoder_1_out14);
  and and_92 (and_92_out, multiplexer_1_out[3], decoder_1_out14);
  not not_45 (not_45_out, multiplexer_1_out[0]);
  and and_93 (and_93_out, not_45_out, decoder_1_out14);
  not not_46 (not_46_out, multiplexer_1_out[1]);
  and and_94 (and_94_out, not_46_out, decoder_1_out14);
  not not_47 (not_47_out, multiplexer_1_out[2]);
  and and_95 (and_95_out, not_47_out, decoder_1_out14);
  not not_48 (not_48_out, multiplexer_1_out[3]);
  and and_96 (and_96_out, not_48_out, decoder_1_out14);
  FlipFlop_JK_Plus flipflop_jk_plus_36 (
    .in_1(and_92_out), .out_5(flipflop_jk_plus_48_out_5[3]), .in_3(or_40_out), .in_4(1'b0), .in_2(CLK));
  or or_33 (or_33_out, Reset, and_71_out);
  or or_34 (or_34_out, Reset, and_72_out);
  FlipFlop_JK_Plus flipflop_jk_plus_37 (
    .in_1(and_67_out), .out_5(flipflop_jk_plus_45_out_5[2]), .in_3(or_33_out), .in_4(1'b0), .in_2(CLK));
  or or_35 (or_35_out, Reset, and_79_out);
  or or_36 (or_36_out, Reset, and_80_out);
  FlipFlop_JK_Plus flipflop_jk_plus_38 (
    .in_1(and_75_out), .out_5(flipflop_jk_plus_46_out_5[2]), .in_3(or_35_out), .in_4(1'b0), .in_2(CLK));
  or or_37 (or_37_out, Reset, and_87_out);
  or or_38 (or_38_out, Reset, and_88_out);
  FlipFlop_JK_Plus flipflop_jk_plus_39 (
    .in_1(and_83_out), .out_5(flipflop_jk_plus_47_out_5[2]), .in_3(or_37_out), .in_4(1'b0), .in_2(CLK));
  or or_39 (or_39_out, Reset, and_95_out);
  or or_40 (or_40_out, Reset, and_96_out);
  FlipFlop_JK_Plus flipflop_jk_plus_40 (
    .in_1(and_91_out), .out_5(flipflop_jk_plus_48_out_5[2]), .in_3(or_39_out), .in_4(1'b0), .in_2(CLK));
  or or_41 (or_41_out, Reset, and_70_out);
  or or_42 (or_42_out, Reset, and_78_out);
  or or_43 (or_43_out, Reset, and_86_out);
  or or_44 (or_44_out, Reset, and_94_out);
  or or_45 (or_45_out, Reset, and_69_out);
  FlipFlop_JK_Plus flipflop_jk_plus_41 (
    .in_1(and_66_out), .out_5(flipflop_jk_plus_45_out_5[1]), .in_3(or_41_out), .in_4(1'b0), .in_2(CLK));
  or or_46 (or_46_out, Reset, and_77_out);
  FlipFlop_JK_Plus flipflop_jk_plus_42 (
    .in_1(and_74_out), .out_5(flipflop_jk_plus_46_out_5[1]), .in_3(or_42_out), .in_4(1'b0), .in_2(CLK));
  or or_47 (or_47_out, Reset, and_85_out);
  FlipFlop_JK_Plus flipflop_jk_plus_43 (
    .in_1(and_82_out), .out_5(flipflop_jk_plus_47_out_5[1]), .in_3(or_43_out), .in_4(1'b0), .in_2(CLK));
  or or_48 (or_48_out, Reset, and_93_out);
  FlipFlop_JK_Plus flipflop_jk_plus_44 (
    .in_1(and_90_out), .out_5(flipflop_jk_plus_48_out_5[1]), .in_3(or_44_out), .in_4(1'b0), .in_2(CLK));
  FlipFlop_JK_Plus flipflop_jk_plus_45 (
    .in_1(and_65_out), .out_5(flipflop_jk_plus_45_out_5[0]), .in_3(or_45_out), .in_4(1'b0), .in_2(CLK));
  FlipFlop_JK_Plus flipflop_jk_plus_46 (
    .in_1(and_73_out), .out_5(flipflop_jk_plus_46_out_5[0]), .in_3(or_46_out), .in_4(1'b0), .in_2(CLK));
  FlipFlop_JK_Plus flipflop_jk_plus_47 (
    .in_1(and_81_out), .out_5(flipflop_jk_plus_47_out_5[0]), .in_3(or_47_out), .in_4(1'b0), .in_2(CLK));
  FlipFlop_JK_Plus flipflop_jk_plus_48 (
    .in_1(and_89_out), .out_5(flipflop_jk_plus_48_out_5[0]), .in_3(or_48_out), .in_4(1'b0), .in_2(CLK));
  and and_97 (and_97_out, multiplexer_1_out[0], decoder_1_out3);
  and and_98 (and_98_out, multiplexer_1_out[1], decoder_1_out3);
  and and_99 (and_99_out, multiplexer_1_out[2], decoder_1_out3);
  and and_100 (and_100_out, multiplexer_1_out[3], decoder_1_out3);
  not not_49 (not_49_out, multiplexer_1_out[0]);
  and and_101 (and_101_out, not_49_out, decoder_1_out3);
  not not_50 (not_50_out, multiplexer_1_out[1]);
  and and_102 (and_102_out, not_50_out, decoder_1_out3);
  not not_51 (not_51_out, multiplexer_1_out[2]);
  and and_103 (and_103_out, not_51_out, decoder_1_out3);
  not not_52 (not_52_out, multiplexer_1_out[3]);
  and and_104 (and_104_out, not_52_out, decoder_1_out3);
  and and_105 (and_105_out, multiplexer_1_out[0], decoder_1_out7);
  and and_106 (and_106_out, multiplexer_1_out[1], decoder_1_out7);
  and and_107 (and_107_out, multiplexer_1_out[2], decoder_1_out7);
  and and_108 (and_108_out, multiplexer_1_out[3], decoder_1_out7);
  not not_53 (not_53_out, multiplexer_1_out[0]);
  and and_109 (and_109_out, not_53_out, decoder_1_out7);
  not not_54 (not_54_out, multiplexer_1_out[1]);
  and and_110 (and_110_out, not_54_out, decoder_1_out7);
  not not_55 (not_55_out, multiplexer_1_out[2]);
  and and_111 (and_111_out, not_55_out, decoder_1_out7);
  not not_56 (not_56_out, multiplexer_1_out[3]);
  and and_112 (and_112_out, not_56_out, decoder_1_out7);
  and and_113 (and_113_out, multiplexer_1_out[0], decoder_1_out11);
  and and_114 (and_114_out, multiplexer_1_out[1], decoder_1_out11);
  and and_115 (and_115_out, multiplexer_1_out[2], decoder_1_out11);
  and and_116 (and_116_out, multiplexer_1_out[3], decoder_1_out11);
  not not_57 (not_57_out, multiplexer_1_out[0]);
  and and_117 (and_117_out, not_57_out, decoder_1_out11);
  not not_58 (not_58_out, multiplexer_1_out[1]);
  and and_118 (and_118_out, not_58_out, decoder_1_out11);
  not not_59 (not_59_out, multiplexer_1_out[2]);
  and and_119 (and_119_out, not_59_out, decoder_1_out11);
  not not_60 (not_60_out, multiplexer_1_out[3]);
  and and_120 (and_120_out, not_60_out, decoder_1_out11);
  and and_121 (and_121_out, multiplexer_1_out[0], decoder_1_out15);
  and and_122 (and_122_out, multiplexer_1_out[1], decoder_1_out15);
  and and_123 (and_123_out, multiplexer_1_out[2], decoder_1_out15);
  and and_124 (and_124_out, multiplexer_1_out[3], decoder_1_out15);
  not not_61 (not_61_out, multiplexer_1_out[0]);
  and and_125 (and_125_out, not_61_out, decoder_1_out15);
  not not_62 (not_62_out, multiplexer_1_out[1]);
  and and_126 (and_126_out, not_62_out, decoder_1_out15);
  not not_63 (not_63_out, multiplexer_1_out[2]);
  and and_127 (and_127_out, not_63_out, decoder_1_out15);
  not not_64 (not_64_out, multiplexer_1_out[3]);
  and and_128 (and_128_out, not_64_out, decoder_1_out15);
  or or_49 (or_49_out, Reset, and_104_out);
  FlipFlop_JK_Plus flipflop_jk_plus_49 (
    .in_1(and_100_out), .out_5(flipflop_jk_plus_61_out_5[3]), .in_3(or_49_out), .in_4(1'b0), .in_2(CLK));
  or or_50 (or_50_out, Reset, and_111_out);
  or or_51 (or_51_out, Reset, and_112_out);
  FlipFlop_JK_Plus flipflop_jk_plus_50 (
    .in_1(and_108_out), .out_5(flipflop_jk_plus_62_out_5[3]), .in_3(or_51_out), .in_4(1'b0), .in_2(CLK));
  or or_52 (or_52_out, Reset, and_119_out);
  or or_53 (or_53_out, Reset, and_120_out);
  FlipFlop_JK_Plus flipflop_jk_plus_51 (
    .in_1(and_116_out), .out_5(flipflop_jk_plus_63_out_5[3]), .in_3(or_53_out), .in_4(1'b0), .in_2(CLK));
  or or_54 (or_54_out, Reset, and_127_out);
  or or_55 (or_55_out, Reset, and_128_out);
  FlipFlop_JK_Plus flipflop_jk_plus_52 (
    .in_1(and_124_out), .out_5(flipflop_jk_plus_64_out_5[3]), .in_3(or_55_out), .in_4(1'b0), .in_2(CLK));
  or or_56 (or_56_out, Reset, and_103_out);
  FlipFlop_JK_Plus flipflop_jk_plus_53 (
    .in_1(and_99_out), .out_5(flipflop_jk_plus_61_out_5[2]), .in_3(or_56_out), .in_4(1'b0), .in_2(CLK));
  FlipFlop_JK_Plus flipflop_jk_plus_54 (
    .in_1(and_107_out), .out_5(flipflop_jk_plus_62_out_5[2]), .in_3(or_50_out), .in_4(1'b0), .in_2(CLK));
  FlipFlop_JK_Plus flipflop_jk_plus_55 (
    .in_1(and_115_out), .out_5(flipflop_jk_plus_63_out_5[2]), .in_3(or_52_out), .in_4(1'b0), .in_2(CLK));
  FlipFlop_JK_Plus flipflop_jk_plus_56 (
    .in_1(and_123_out), .out_5(flipflop_jk_plus_64_out_5[2]), .in_3(or_54_out), .in_4(1'b0), .in_2(CLK));
  or or_57 (or_57_out, Reset, and_102_out);
  FlipFlop_JK_Plus flipflop_jk_plus_57 (
    .in_1(and_98_out), .out_5(flipflop_jk_plus_61_out_5[1]), .in_3(or_57_out), .in_4(1'b0), .in_2(CLK));
  or or_58 (or_58_out, Reset, and_110_out);
  FlipFlop_JK_Plus flipflop_jk_plus_58 (
    .in_1(and_106_out), .out_5(flipflop_jk_plus_62_out_5[1]), .in_3(or_58_out), .in_4(1'b0), .in_2(CLK));
  or or_59 (or_59_out, Reset, and_118_out);
  FlipFlop_JK_Plus flipflop_jk_plus_59 (
    .in_1(and_114_out), .out_5(flipflop_jk_plus_63_out_5[1]), .in_3(or_59_out), .in_4(1'b0), .in_2(CLK));
  or or_60 (or_60_out, Reset, and_126_out);
  FlipFlop_JK_Plus flipflop_jk_plus_60 (
    .in_1(and_122_out), .out_5(flipflop_jk_plus_64_out_5[1]), .in_3(or_60_out), .in_4(1'b0), .in_2(CLK));
  or or_61 (or_61_out, Reset, and_101_out);
  FlipFlop_JK_Plus flipflop_jk_plus_61 (
    .in_1(and_97_out), .out_5(flipflop_jk_plus_61_out_5[0]), .in_3(or_61_out), .in_4(1'b0), .in_2(CLK));
  or or_62 (or_62_out, Reset, and_109_out);
  FlipFlop_JK_Plus flipflop_jk_plus_62 (
    .in_1(and_105_out), .out_5(flipflop_jk_plus_62_out_5[0]), .in_3(or_62_out), .in_4(1'b0), .in_2(CLK));
  or or_63 (or_63_out, Reset, and_117_out);
  FlipFlop_JK_Plus flipflop_jk_plus_63 (
    .in_1(and_113_out), .out_5(flipflop_jk_plus_63_out_5[0]), .in_3(or_63_out), .in_4(1'b0), .in_2(CLK));
  or or_64 (or_64_out, Reset, and_125_out);
  FlipFlop_JK_Plus flipflop_jk_plus_64 (
    .in_1(and_121_out), .out_5(flipflop_jk_plus_64_out_5[0]), .in_3(or_64_out), .in_4(1'b0), .in_2(CLK));
  Multiplexer #(.select(4), .width(4)) multiplexer_2 (
    .in0(flipflop_jk_plus_13_out_5), .in1(flipflop_jk_plus_29_out_5), .in2(flipflop_jk_plus_45_out_5),
    .in3(flipflop_jk_plus_61_out_5), .in4(flipflop_jk_plus_14_out_5), .in5(flipflop_jk_plus_30_out_5),
    .in6(flipflop_jk_plus_46_out_5), .in7(flipflop_jk_plus_62_out_5), .in8(flipflop_jk_plus_15_out_5),
    .in9(flipflop_jk_plus_31_out_5), .in10(flipflop_jk_plus_47_out_5), .in11(flipflop_jk_plus_63_out_5),
    .in12(flipflop_jk_plus_16_out_5), .in13(flipflop_jk_plus_32_out_5), .in14(flipflop_jk_plus_48_out_5),
    .in15(flipflop_jk_plus_64_out_5), .out(out_6), .sel(Adress));  // open: en
  // AND_Gate and_129 is placed but not wired
  // AND_Gate and_130 is placed but not wired
endmodule

module teste_codificador_e_multiplexador (
  output out_1
);

  wire [3:0] undriven;
  wire [3:1] multiplexer_1_out;

  Button button_1 ();  // open: out
  Multiplexer #(.select(4), .width(4)) multiplexer_1 (.out({multiplexer_1_out, out_1}));  // open: in0, in1, in2, in3, in4, in5, in6, in7, in8, in9, in10, in11, in12, in13, in14, in15, sel, en
  Button button_2 ();  // open: out
  Decoder #(.select(4)) decoder_1 (.sel(undriven));  // open: out0, out1, out2, out3, out4, out5, out6, out7, out8, out9, out10, out11, out12, out13, out14, out15, en
  // Pins of 1 and 4 bits meet at {multiplexer_1_out, out_1}
endmodule

module Animacao_morte (
  input  in_1,
  input  in_2,
  output T,
  output R,
  output S,
  output [3:0] Y,
  output out_7
);

  wire and_1_out, and_2_out, and_3_out, and_4_out, and_5_out, and_6_out, and_7_out, and_8_out, and_9_out,
       and_10_out, and_11_out, and_12_out, and_13_out, d_ff_1_q, j_k_ff_1_q, j_k_ff_2_q, j_k_ff_3_q,
       multiplexer_1_out, not_1_out, not_2_out, not_3_out, not_4_out, not_5_out, not_6_out, not_7_out,
       not_8_out, not_9_out, not_10_out, not_11_out, not_12_out, not_13_out, not_14_out, not_15_out,
       not_16_out, not_17_out, not_18_out, not_19_out, not_20_out, not_21_out, not_22_out, not_23_out,
       not_24_out, not_25_out, not_26_out, not_27_out, not_28_out, not_29_out, or_1_out, or_2_out, or_4_out;
  wire [1:0] counter_3_q;
  wire [3:0] \codificador_do_display_1_y₀ , \codificador_do_display_1_y₁ , \codificador_do_display_1_y₂ ,
       \codificador_do_display_1_y₃ ;
  wire [7:0] counter_2_q;

  and and_1 (and_1_out, in_1, in_2);
  Counter #(.width(4), .max('hf)) counter_1 (.Q(Y), .clk(and_1_out), .clr(d_ff_1_q));  // open: load, D, count, carry
  and and_2 (and_2_out, and_1_out, j_k_ff_1_q);
  and and_3 (and_3_out, Y[0], Y[1], Y[2], Y[3]);
  Counter counter_2 (.Q(counter_2_q), .clk(and_2_out));  // open: load, D, count, carry, clr
  not not_1 (not_1_out, Y[1]);
  and and_4 (and_4_out, Y[0], not_1_out, Y[2], not_2_out);
  not not_2 (not_2_out, Y[3]);
  not not_3 (not_3_out, Y[0]);
  and and_5 (and_5_out, not_3_out, Y[1], Y[2], not_4_out);
  not not_4 (not_4_out, Y[3]);
  not not_5 (not_5_out, Y[1]);
  and and_6 (and_6_out, Y[0], not_5_out, not_6_out, Y[3]);
  not not_6 (not_6_out, Y[2]);
  not not_7 (not_7_out, Y[0]);
  and and_7 (and_7_out, not_7_out, Y[1], not_8_out, Y[3]);
  not not_8 (not_8_out, Y[2]);
  not not_9 (not_9_out, j_k_ff_1_q);
  J_K_Flip_Flop j_k_ff_1 (.J(and_3_out), .clk(and_1_out), .K(d_ff_1_q), .Q(j_k_ff_1_q));  // open: Qn, preset, en, reset
  or or_1 (or_1_out, and_4_out, and_5_out, and_6_out, and_7_out);
  not not_10 (not_10_out, counter_2_q[0]);
  not not_11 (not_11_out, counter_2_q[1]);
  not not_12 (not_12_out, counter_2_q[2]);
  not not_13 (not_13_out, counter_2_q[3]);
  not not_14 (not_14_out, counter_2_q[4]);
  not not_15 (not_15_out, counter_2_q[5]);
  not not_16 (not_16_out, counter_2_q[6]);
  not not_17 (not_17_out, counter_2_q[7]);
  not not_18 (not_18_out, counter_2_q[0]);
  not not_19 (not_19_out, counter_2_q[1]);
  not not_20 (not_20_out, counter_2_q[2]);
  not not_21 (not_21_out, counter_2_q[3]);
  not not_22 (not_22_out, counter_2_q[4]);
  not not_23 (not_23_out, counter_2_q[5]);
  not not_24 (not_24_out, counter_2_q[6]);
  not not_25 (not_25_out, counter_2_q[4]);
  not not_26 (not_26_out, or_1_out);
  Multiplexer multiplexer_1 (.in0(not_26_out), .in1(or_1_out), .out(multiplexer_1_out), .sel(j_k_ff_3_q));  // open: en
  and and_8 (and_8_out, not_10_out, not_11_out, not_12_out, not_13_out, not_14_out, not_15_out, not_16_out, not_17_out);
  and and_9 (and_9_out, counter_2_q[0], counter_2_q[1], counter_2_q[2], counter_2_q[3], not_27_out, counter_2_q[5], counter_2_q[6], not_28_out);
  not not_27 (not_27_out, counter_2_q[4]);
  not not_28 (not_28_out, counter_2_q[7]);
  and and_10 (and_10_out, not_18_out, not_19_out, not_20_out, not_21_out, not_22_out, not_23_out, not_24_out, counter_2_q[7]);
  and and_11 (and_11_out, counter_2_q[0], counter_2_q[1], counter_2_q[2], counter_2_q[3], not_25_out, counter_2_q[5], counter_2_q[6], counter_2_q[7]);
  and and_12 (and_12_out, counter_2_q[0], counter_2_q[1], counter_2_q[2], counter_2_q[3], counter_2_q[4], counter_2_q[5], counter_2_q[6], counter_2_q[7]);
  not not_29 (not_29_out, j_k_ff_2_q);
  or or_2 (or_2_out, and_9_out, and_11_out);
  or or_3 (R, not_9_out, and_13_out);
  and and_13 (and_13_out, multiplexer_1_out, not_29_out);
  and and_14 (S, multiplexer_1_out, j_k_ff_2_q);
  or or_4 (or_4_out, and_8_out, and_10_out);
  Counter #(.width(2), .max('h3)) counter_3 (
    .Q(counter_3_q), .clk(and_12_out), .clr(d_ff_1_q));  // open: load, D, count, carry
  J_K_Flip_Flop j_k_ff_2 (.J(or_4_out), .clk(and_1_out), .K(or_2_out), .Q(j_k_ff_2_q));  // open: Qn, preset, en, reset
  J_K_Flip_Flop j_k_ff_3 (
    .J(and_8_out), .clk(and_1_out), .K(and_10_out), .Q(j_k_ff_3_q));  // open: Qn, preset, en, reset
  and and_15 (out_7, counter_3_q[0], counter_3_q[1]);
  D_Flip_Flop d_ff_1 (.clk(in_2), .D(out_7), .Q(d_ff_1_q));  // open: Qn, preset, en, reset
  Codificador_do_display codificador_do_display_1 (
    .\Y₃ (\codificador_do_display_1_y₃ ), .\Y₂ (\codificador_do_display_1_y₂ ),
    .\Y₁ (\codificador_do_display_1_y₁ ), .\Y₀ (\codificador_do_display_1_y₀ ), .T(1'b0));  // open: X, CLK, S, R, write_enable, in_7, out_12
  DotMatrix #(.matrixcols(4), .matrixrows(4)) dotmatrix_1 (
    .col0(\codificador_do_display_1_y₀ ), .col1(\codificador_do_display_1_y₁ ),
    .col2(\codificador_do_display_1_y₂ ), .col3(\codificador_do_display_1_y₃ ));
  // AND_Gate and_16 is placed but not wired

  assign T = 1'b0;
endmodule

module Definir_posicoes_iniciais (
  input  in_1,
  input  in_2
);

  wire and_1_out, and_2_out;
  wire [3:0] random_1_out, random_2_out, xnor_1_out;

  Random #(.width(4)) random_1 (.clk(and_1_out), .out(random_1_out));  // open: next, clr
  and and_1 (and_1_out, in_1, in_2);
  Random #(.width(4)) random_2 (.clk(and_1_out), .out(random_2_out));  // open: next, clr
  assign xnor_1_out = ~(random_1_out ^ random_2_out);  // XNOR_Gate xnor_1, 4 bits wide
  and and_2 (and_2_out, xnor_1_out[0], xnor_1_out[1], xnor_1_out[2], xnor_1_out[3]);
endmodule

module Calculo_nova_posicao (
  input  [3:0] in_1,
  input  [1:0] in_2,
  output [3:0] out_3
);

  wire and_1_out, and_2_out, and_3_out, and_4_out, not_1_out, not_2_out, not_3_out, not_4_out;
  wire [3:0] adder_1_out, adder_2_out, adder_3_out, adder_4_out, multiplexer_1_out, multiplexer_2_out,
       multiplexer_3_out, multiplexer_4_out, subtractor_1_out, subtractor_2_out, subtractor_3_out,
       subtractor_4_out;

  Subtractor #(.width(4)) subtractor_1 (.a(in_1), .b(4'b0100), .out(subtractor_1_out));  // open: bin, bout
  Adder #(.width(4)) adder_1 (.a(in_1), .b(4'b1100), .out(adder_1_out));  // open: cin, cout
  not not_1 (not_1_out, in_1[2]);
  and and_1 (and_1_out, not_1_out, not_2_out);
  not not_2 (not_2_out, in_1[3]);
  Subtractor #(.width(4)) subtractor_2 (.a(in_1), .b(4'b0001), .out(subtractor_2_out));  // open: bin, bout
  Adder #(.width(4)) adder_2 (.a(in_1), .b(4'b0011), .out(adder_2_out));  // open: cin, cout
  not not_3 (not_3_out, in_1[0]);
  and and_2 (and_2_out, not_3_out, not_4_out);
  not not_4 (not_4_out, in_1[1]);
  Adder #(.width(4)) adder_3 (.a(in_1), .b(4'b0100), .out(adder_3_out));  // open: cin, cout
  Subtractor #(.width(4)) subtractor_3 (.a(in_1), .b(4'b1100), .out(subtractor_3_out));  // open: bin, bout
  and and_3 (and_3_out, in_1[0], in_1[1]);
  Adder #(.width(4)) adder_4 (.a(in_1), .b(4'b0001), .out(adder_4_out));  // open: cin, cout
  Subtractor #(.width(4)) subtractor_4 (.a(in_1), .b(4'b0011), .out(subtractor_4_out));  // open: bin, bout
  and and_4 (and_4_out, in_1[0], in_1[1]);
  Multiplexer #(.width(4)) multiplexer_1 (
    .in0(subtractor_1_out), .in1(adder_1_out), .out(multiplexer_1_out), .sel(and_1_out));  // open: en
  Multiplexer #(.width(4)) multiplexer_2 (
    .in0(subtractor_2_out), .in1(adder_2_out), .out(multiplexer_2_out), .sel(and_2_out));  // open: en
  Multiplexer #(.width(4)) multiplexer_3 (
    .in0(adder_3_out), .in1(subtractor_3_out), .out(multiplexer_3_out), .sel(and_3_out));  // open: en
  Multiplexer #(.width(4)) multiplexer_4 (
    .in0(adder_4_out), .in1(subtractor_4_out), .out(multiplexer_4_out), .sel(and_4_out));  // open: en
  Multiplexer #(.select(2), .width(4)) multiplexer_5 (
    .in0(multiplexer_1_out), .in1(multiplexer_2_out), .in2(multiplexer_3_out), .in3(multiplexer_4_out),
    .out(out_3), .sel(in_2));  // open: en
  // AND_Gate and_5 is placed but not wired
  // AND_Gate and_6 is placed but not wired

  // Notes on the sheet:
  //   cima
  //   esquerda
  //   baixo
  //   direita
endmodule

module Teste_de_controlador (
  input  in_1,
  input  in_2,
  input  in_3,
  input  in_4,
  input  in_5,
  input  in_6
);

  wire and_1_out, and_2_out, and_3_out, and_4_out, and_5_out, and_6_out, and_7_out, and_8_out, and_9_out,
       and_10_out, and_11_out, and_13_out, and_14_out, animacao_morte_1_out_7, button_1_out, button_2_out,
       button_3_out, button_4_out, clock_1_out, codificador_do_display_1_out_12, counter_1_q, counter_4_q,
       d_ff_3_q, d_ff_4_q, d_ff_5_q, not_1_out, not_2_out, not_3_out, not_4_out, not_5_out, not_6_out,
       not_7_out, not_8_out, not_9_out, not_10_out, not_11_out, not_12_out, not_13_out, not_14_out,
       not_15_out;
  wire [0:0] and_12_out, j_k_ff_1_q;
  wire [1:0] d_ff_1_q;
  wire [2:0] animacao_morte_1_t, \input ;
  wire [3:0] adder_1_out, adder_2_out, animacao_morte_1_y, \codificador_do_display_1_y₀ ,
       \codificador_do_display_1_y₁ , \codificador_do_display_1_y₂ , \codificador_do_display_1_y₃ ,
       Comida_out_6, counter_3_q, \Estado_da_máquina_out_6 , \lista_de_memória_1_out_6 ,
       \lista_de_memória_2_out_6 , multiplexer_1_out, multiplexer_2_out, multiplexer_3_out,
       multiplexer_4_out, multiplexer_6_out, multiplexer_7_out, multiplexer_9_out, multiplexer_10_out,
       multiplexer_12_out, multiplexer_15_out, multiplexer_16_out, Ponteiro_cabeca_out_6,
       Ponteiro_cauda_out_6, random_1_out, random_2_out, random_3_out, subtractor_1_out, subtractor_2_out,
       xnor_1_out, xnor_2_out, xnor_3_out, xnor_4_out;
  wire [5:0] multiplexer_8_out, multiplexer_11_out, multiplexer_13_out;
  wire [6:3] Posicoes_da_cobrinha_out_6;
  wire [7:0] counter_2_q;
  wire [7:4] calculo_nova_posicao_1_out_3;
  wire [9:0] multiplexer_5_out;
  wire [11:0] multiplexer_14_out, multiplexer_17_out;

  not not_1 (not_1_out, in_1);
  Random #(.width(4)) random_1 (.clk(clock_1_out), .out(random_1_out));  // open: next, clr
  Random #(.width(4), .seed(1)) random_2 (.clk(clock_1_out), .out(random_2_out));  // open: next, clr
  not not_2 (not_2_out, and_1_out);
  and and_1 (and_1_out, \Estado_da_máquina_out_6 [0], \Estado_da_máquina_out_6 [1], not_3_out, not_4_out);
  not not_3 (not_3_out, \Estado_da_máquina_out_6 [2]);
  not not_4 (not_4_out, \Estado_da_máquina_out_6 [3]);
  J_K_Flip_Flop j_k_ff_1 (
    .J(in_1), .clk(clock_1_out), .K(not_1_out), .Q(j_k_ff_1_q[0]));  // open: Qn, preset, en, reset
  assign xnor_1_out = ~(random_1_out ^ random_2_out);  // XNOR_Gate xnor_1, 4 bits wide
  Counter #(.width(1), .max('h1)) counter_1 (
    .Q(counter_1_q), .clk(clock_1_out), .clr(\Estado_da_máquina_out_6 [0]));  // open: load, D, count, carry
  Counter counter_2 (.Q(counter_2_q), .clk(clock_1_out), .clr(not_2_out));  // open: load, D, count, carry
  and and_2 (and_2_out, xnor_1_out[0], xnor_1_out[1], xnor_1_out[2], xnor_1_out[3]);
  D_Flip_Flop d_ff_1 (.clk(\input [0]), .D(\input [1]), .Q(d_ff_1_q[0]));  // open: Qn, preset, en, reset
  D_Flip_Flop d_ff_2 (.clk(\input [0]), .D(\input [2]), .Q(d_ff_1_q[1]));  // open: Qn, preset, en, reset
  Multiplexer #(.width(4)) multiplexer_1 (
    .in0(4'b0010), .in1(4'b0001), .out(multiplexer_1_out), .sel(and_2_out));  // open: en
  Multiplexer #(.width(4)) multiplexer_2 (
    .in0(4'b0010), .in1(4'b0011), .out(multiplexer_2_out), .sel(counter_1_q));  // open: en
  and and_3 (and_3_out, counter_2_q[0], counter_2_q[1], counter_2_q[2], counter_2_q[3], counter_2_q[4], counter_2_q[5], counter_2_q[6], counter_2_q[7]);
  Multiplexer #(.width(4)) multiplexer_3 (
    .in0(4'b0011), .in1(4'b0100), .out(multiplexer_3_out), .sel(and_3_out));  // open: en
  Multiplexer #(.select(4), .width(4)) multiplexer_4 (
    .in0({3'b000, j_k_ff_1_q[0]}), .in1(multiplexer_1_out), .in2(multiplexer_2_out), .in3(4'b0100),
    .in4(4'b0101), .in5(multiplexer_9_out), .in6(4'b0111), .in7(multiplexer_12_out), .in8(4'b1001),
    .in9(multiplexer_10_out), .in10(4'b0011), .in14(multiplexer_16_out), .out(multiplexer_4_out),
    .sel(\Estado_da_máquina_out_6 ));  // open: in11, in12, in13, in15, en
  not not_5 (not_5_out, \Estado_da_máquina_out_6 [0]);
  not not_6 (not_6_out, \Estado_da_máquina_out_6 [1]);
  not not_7 (not_7_out, \Estado_da_máquina_out_6 [3]);
  \Lista_de_memória  \Estado_da_máquina  (
    .Adress(4'b0000), .Writing(multiplexer_4_out), .Write_enable(1'b1), .Reset(1'b0), .CLK(clock_1_out),
    .out_6(\Estado_da_máquina_out_6 ));
  and and_4 (and_4_out, not_5_out, not_6_out, \Estado_da_máquina_out_6 [2], not_7_out);
  \Lista_de_memória  \lista_de_memória_1  (
    .Adress(4'b0000), .Writing(Posicoes_da_cobrinha_out_6), .Write_enable(and_4_out), .Reset(1'b0),
    .CLK(clock_1_out), .out_6(\lista_de_memória_1_out_6 ));
  Calculo_nova_posicao calculo_nova_posicao_1 (
    .in_1(\lista_de_memória_1_out_6 ), .in_2(d_ff_1_q), .out_3(calculo_nova_posicao_1_out_3));
  not not_8 (not_8_out, \Estado_da_máquina_out_6 [1]);
  and and_5 (and_5_out, \Estado_da_máquina_out_6 [0], not_8_out, \Estado_da_máquina_out_6 [2], not_9_out);
  not not_9 (not_9_out, \Estado_da_máquina_out_6 [3]);
  Multiplexer #(.select(4), .width(10)) multiplexer_5 (
    .in1({2'b01, random_1_out, 4'b0000}), .in2({10{1'b0}}), .in4({{6{1'b0}}, Ponteiro_cabeca_out_6}),
    .in5({{6{1'b0}}, subtractor_1_out}), .in6({2'b01, calculo_nova_posicao_1_out_3, adder_1_out}),
    .in7({{6{1'b0}}, multiplexer_15_out}), .in8({2'b01, calculo_nova_posicao_1_out_3, adder_1_out}),
    .out(multiplexer_5_out), .sel(\Estado_da_máquina_out_6 ));  // open: in0, in3, in9, in10, in11, in12, in13, in14, in15, en
  Counter #(.width(4), .max('hf)) counter_3 (
    .Q(counter_3_q), .clk(and_6_out), .clr(d_ff_4_q));  // open: load, D, count, carry
  and and_6 (and_6_out, clock_1_out, d_ff_3_q);
  D_Flip_Flop d_ff_3 (.clk(clock_1_out), .D(and_7_out), .Q(d_ff_3_q));  // open: Qn, preset, en, reset
  and and_7 (and_7_out, and_5_out, not_10_out);
  and and_8 (and_8_out, and_5_out, and_11_out);
  not not_10 (not_10_out, and_11_out);
  Subtractor #(.width(4)) subtractor_1 (
    .a(Ponteiro_cabeca_out_6), .b(counter_3_q), .out(subtractor_1_out));  // open: bin, bout
  D_Flip_Flop d_ff_4 (.clk(clock_1_out), .D(and_8_out), .Q(d_ff_4_q));  // open: Qn, preset, en, reset
  \Lista_de_memória  Posicoes_da_cobrinha (
    .Adress(multiplexer_5_out[3:0]), .Writing(multiplexer_5_out[7:4]), .Write_enable(multiplexer_5_out[8]),
    .Reset(multiplexer_5_out[9]), .CLK(clock_1_out), .out_6(Posicoes_da_cobrinha_out_6));
  assign xnor_2_out = ~(Posicoes_da_cobrinha_out_6 ^ calculo_nova_posicao_1_out_3);  // XNOR_Gate xnor_2, 4 bits wide
  assign xnor_3_out = ~(Comida_out_6 ^ calculo_nova_posicao_1_out_3);  // XNOR_Gate xnor_3, 4 bits wide
  assign xnor_4_out = ~(Ponteiro_cauda_out_6 ^ subtractor_1_out);  // XNOR_Gate xnor_4, 4 bits wide
  and and_9 (and_9_out, xnor_2_out[0], xnor_2_out[1], xnor_2_out[2], xnor_2_out[3]);
  Multiplexer #(.width(4)) multiplexer_6 (
    .in0(4'b0110), .in1(4'b1000), .out(multiplexer_6_out), .sel(and_10_out));  // open: en
  and and_10 (and_10_out, xnor_3_out[0], xnor_3_out[1], xnor_3_out[2], xnor_3_out[3]);
  and and_11 (and_11_out, xnor_4_out[0], xnor_4_out[1], xnor_4_out[2], xnor_4_out[3]);
  Random #(.width(4)) random_3 (.clk(clock_1_out), .out(random_3_out));  // open: next, clr
  Multiplexer #(.width(4)) multiplexer_7 (
    .in0(4'b0101), .in1(multiplexer_6_out), .out(multiplexer_7_out), .sel(and_11_out));  // open: en
  Multiplexer #(.select(4), .width(6)) multiplexer_8 (
    .in1(6'b010000), .in6({2'b01, adder_1_out}), .in8({2'b01, adder_1_out}), .out(multiplexer_8_out),
    .sel(\Estado_da_máquina_out_6 ));  // open: in0, in2, in3, in4, in5, in7, in9, in10, in11, in12, in13, in14, in15, en
  Multiplexer #(.width(4)) multiplexer_9 (
    .in0(multiplexer_7_out), .in1(4'b1110), .out(multiplexer_9_out), .sel(and_9_out));  // open: en
  not not_11 (not_11_out, codificador_do_display_1_out_12);
  \Lista_de_memória  \lista_de_memória_2  (
    .Adress(4'b0000), .Writing(random_3_out), .Write_enable(not_11_out), .Reset(1'b0), .CLK(clock_1_out),
    .out_6(\lista_de_memória_2_out_6 ));
  \Lista_de_memória  Ponteiro_cabeca (
    .Adress(4'b0000), .Writing(multiplexer_8_out[3:0]), .Write_enable(multiplexer_8_out[4]),
    .Reset(multiplexer_8_out[5]), .CLK(clock_1_out), .out_6(Ponteiro_cabeca_out_6));
  Multiplexer #(.width(4)) multiplexer_10 (
    .in0(4'b1001), .in1(4'b1010), .out(multiplexer_10_out), .sel(not_11_out));  // open: en
  Adder #(.width(4)) adder_1 (.a(Ponteiro_cabeca_out_6), .b(4'b0001), .out(adder_1_out));  // open: cin, cout
  Multiplexer #(.select(4), .width(6)) multiplexer_11 (
    .in1(6'b010000), .in6({2'b01, adder_2_out}), .out(multiplexer_11_out), .sel(\Estado_da_máquina_out_6 ));  // open: in0, in2, in3, in4, in5, in7, in8, in9, in10, in11, in12, in13, in14, in15, en
  Adder #(.width(4)) adder_2 (.a(Ponteiro_cauda_out_6), .b(4'b0001), .out(adder_2_out));  // open: cin, cout
  \Lista_de_memória  Ponteiro_cauda (
    .Adress(4'b0000), .Writing(multiplexer_11_out[3:0]), .Write_enable(multiplexer_11_out[4]),
    .Reset(multiplexer_11_out[5]), .CLK(clock_1_out), .out_6(Ponteiro_cauda_out_6));
  D_Flip_Flop d_ff_5 (.clk(clock_1_out), .D(counter_2_q[5]), .Q(d_ff_5_q));  // open: Qn, preset, en, reset
  not not_12 (not_12_out, \Estado_da_máquina_out_6 [3]);
  and and_12 (and_12_out[0], counter_2_q[5], not_13_out);
  not not_13 (not_13_out, d_ff_5_q);
  Counter #(.width(1), .max('h1)) counter_4 (
    .Q(counter_4_q), .clk(clock_1_out), .clr(not_14_out));  // open: load, D, count, carry
  not not_14 (not_14_out, and_13_out);
  and and_13 (and_13_out, \Estado_da_máquina_out_6 [0], \Estado_da_máquina_out_6 [1], \Estado_da_máquina_out_6 [2], not_12_out);
  Multiplexer #(.width(4)) multiplexer_12 (
    .in0(4'b0111), .in1(4'b0011), .out(multiplexer_12_out), .sel(counter_4_q));  // open: en
  Multiplexer #(.select(4), .width(6)) multiplexer_13 (
    .in1({2'b01, random_2_out}), .in10({2'b01, \lista_de_memória_2_out_6 }), .out(multiplexer_13_out),
    .sel(\Estado_da_máquina_out_6 ));  // open: in0, in2, in3, in4, in5, in6, in7, in8, in9, in11, in12, in13, in14, in15, en
  \Lista_de_memória  Comida (
    .Adress(4'b0000), .Writing(multiplexer_13_out[3:0]), .Write_enable(multiplexer_13_out[4]),
    .Reset(multiplexer_13_out[5]), .CLK(clock_1_out), .out_6(Comida_out_6));
  Multiplexer #(.width(12)) multiplexer_14 (
    .in0({5'b00001, Comida_out_6, 3'b100}), .in1({5'b00001, Posicoes_da_cobrinha_out_6, 3'b100}),
    .out(multiplexer_14_out), .sel(counter_1_q));  // open: en
  not not_15 (not_15_out, \Estado_da_máquina_out_6 [0]);
  and and_14 (and_14_out, not_15_out, \Estado_da_máquina_out_6 [1], \Estado_da_máquina_out_6 [2], \Estado_da_máquina_out_6 [3]);
  Clock clock_1 (.out(clock_1_out));
  Subtractor #(.width(4)) subtractor_2 (
    .a(Ponteiro_cauda_out_6), .b(4'b0001), .out(subtractor_2_out));  // open: bin, bout
  Multiplexer #(.width(4)) multiplexer_15 (
    .in0(subtractor_2_out), .in1(Ponteiro_cabeca_out_6), .out(multiplexer_15_out), .sel(counter_4_q),
    .en(and_13_out));
  Button button_1 (.out(button_1_out));
  Button button_2 (.out(button_2_out));
  Button button_3 (.out(button_3_out));
  Button button_4 (.out(button_4_out));
  Animacao_morte animacao_morte_1 (
    .in_1(and_14_out), .in_2(clock_1_out), .T(animacao_morte_1_t[0]), .R(animacao_morte_1_t[1]),
    .S(animacao_morte_1_t[2]), .Y(animacao_morte_1_y), .out_7(animacao_morte_1_out_7));
  or or_1 (\input [0], button_1_out, button_2_out, button_3_out, button_4_out);
  or or_2 (\input [1], button_2_out, button_4_out);
  or or_3 (\input [2], button_4_out, button_3_out);
  Multiplexer #(.width(4)) multiplexer_16 (
    .in0(4'b1110), .in1(4'b0000), .out(multiplexer_16_out), .sel(animacao_morte_1_out_7));  // open: en
  Multiplexer #(.select(4), .width(12)) multiplexer_17 (
    .in2(multiplexer_14_out), .in3({5'b00001, Comida_out_6, 2'b00, and_12_out[0]}),
    .in7({5'b00001, Posicoes_da_cobrinha_out_6, 3'b001}), .in9({random_3_out, {8{1'b0}}}),
    .in10({5'b00001, \lista_de_memória_2_out_6 , 3'b100}),
    .in14({5'b00001, animacao_morte_1_y, animacao_morte_1_t}), .out(multiplexer_17_out),
    .sel(\Estado_da_máquina_out_6 ));  // open: in0, in1, in4, in5, in6, in8, in11, in12, in13, in15, en
  Codificador_do_display codificador_do_display_1 (
    .X(multiplexer_17_out[6:3]), .CLK(clock_1_out), .\Y₃ (\codificador_do_display_1_y₃ ),
    .\Y₂ (\codificador_do_display_1_y₂ ), .\Y₁ (\codificador_do_display_1_y₁ ),
    .\Y₀ (\codificador_do_display_1_y₀ ), .S(multiplexer_17_out[2]), .R(multiplexer_17_out[1]),
    .T(multiplexer_17_out[0]), .write_enable(multiplexer_17_out[7]), .in_7(multiplexer_17_out[11:8]),
    .out_12(codificador_do_display_1_out_12));
  DotMatrix #(.matrixcols(4), .matrixrows(4)) dotmatrix_1 (
    .col0(\codificador_do_display_1_y₀ ), .col1(\codificador_do_display_1_y₁ ),
    .col2(\codificador_do_display_1_y₂ ), .col3(\codificador_do_display_1_y₃ ));
  // AND_Gate and_15 is placed but not wired
  // AND_Gate and_16 is placed but not wired

  // Other names for the same wires on the sheet: CLK = in_6

  // Notes on the sheet:
  //   teste
  //   teste
  //   teste
  //   teste
  //   teste
  //   teste
  //   teste
  //   teste
  //   teste
  //   teste
  //   teste
  //   teste
  //   teste
  //   teste
  //   teste
  //   teste
  //   teste
endmodule
